// Logisim project baranov1.circ as structural Verilog: 44 circuits, main circuit byte AND
module byte_AND (
  input  [7:0] in_1,
  input  [7:0] in_2,
  output [7:0] out_3
);

  assign out_3 = in_1 & in_2;  // AND_Gate and_1, 8 bits wide
endmodule

module byte_OR (
  input  [7:0] in_1,
  input  [7:0] in_2,
  output [7:0] out_3
);

  assign out_3 = in_1 | in_1 | in_2;  // OR_Gate or_1, 8 bits wide

  // Notes on the sheet:
  //   TIMOFEENKO
endmodule

module byte_XOR (
  input  [7:0] in_1,
  input  [7:0] in_2,
  output [7:0] out_3
);

  assign out_3 = in_1 ^ in_2;  // XOR_Gate xor_1, 8 bits wide

  // Notes on the sheet:
  //   TIMOFEENKO
endmodule

module byte_NOT (
  input  [7:0] in_1,
  output [7:0] out_2
);

  assign out_2 = ~in_1;  // NOT_Gate not_1, 8 bits wide

  // Notes on the sheet:
  //   TIMOFEENKO
endmodule

module logical_AND (
  input  [7:0] in_1,
  input  [7:0] in_2,
  output out_3
);

  wire or_1_out, or_2_out;

  or or_1 (or_1_out, in_1[0], in_1[1], in_1[2], in_1[3], in_1[4], in_1[5], in_1[6], in_1[7]);
  or or_2 (or_2_out, in_2[0], in_2[1], in_2[2], in_2[3], in_2[4], in_2[5], in_2[6], in_2[7]);
  and and_1 (out_3, or_1_out, or_2_out);

  // Notes on the sheet:
  //   TIMOFEENKO
endmodule

module logical_OR (
  input  [7:0] in_1,
  input  [7:0] in_2,
  output out_3
);

  wire or_1_out, or_2_out;

  or or_1 (or_1_out, in_1[0], in_1[1], in_1[2], in_1[3], in_1[4], in_1[5], in_1[6], in_1[7]);
  or or_2 (or_2_out, in_2[0], in_2[1], in_2[2], in_2[3], in_2[4], in_2[5], in_2[6], in_2[7]);
  or or_3 (out_3, or_1_out, or_2_out);

  // Notes on the sheet:
  //   TIMOFEENKO
endmodule

module logical_XOR (
  input  [7:0] in_1,
  input  [7:0] in_2,
  output out_3
);

  wire or_1_out, or_2_out;

  or or_1 (or_1_out, in_1[0], in_1[1], in_1[2], in_1[3], in_1[4], in_1[5], in_1[6], in_1[7]);
  or or_2 (or_2_out, in_2[0], in_2[1], in_2[2], in_2[3], in_2[4], in_2[5], in_2[6], in_2[7]);
  xor xor_1 (out_3, or_1_out, or_2_out);

  // Notes on the sheet:
  //   TIMOFEENKO
endmodule

module logical_NOT (
  input  [7:0] in_1,
  output out_2
);

  wire [7:0] byte_not_1_out_2;

  byte_NOT byte_not_1 (.in_1(in_1), .out_2(byte_not_1_out_2));
  or or_1 (out_2, byte_not_1_out_2[0], byte_not_1_out_2[1], byte_not_1_out_2[2], byte_not_1_out_2[3], byte_not_1_out_2[4], byte_not_1_out_2[5], byte_not_1_out_2[6], byte_not_1_out_2[7]);

  // Notes on the sheet:
  //   TIMOFEENKO
endmodule

module logical_shr_1_bit (
  input  [7:0] in_1,
  output [7:0] out_2
);


  assign out_2 = {1'b0, in_1[7:1]};
endmodule

module logical_shl_1_bit (
  input  [7:0] in_1,
  output [7:0] out_2
);


  assign out_2 = {in_1[6:0], 1'b0};
endmodule

module arifmetical_shr_1_bit (
  input  [7:0] in_1,
  output [7:0] out_2
);


  assign out_2 = {{2{in_1[7]}}, in_1[6:1]};
endmodule

module arifmetical_shl_1_bit (
  input  [7:0] in_1,
  output [7:0] out_2
);


  assign out_2 = {in_1[6:0], in_1[0]};
endmodule

module circular_shr_1_bit (
  input  [7:0] in_1,
  output [7:0] out_2
);


  assign out_2 = {in_1[0], in_1[7:1]};
endmodule

module curcular_shl_1_bit (
  input  [7:0] in_1,
  output [7:0] out_2
);


  assign out_2 = {in_1[6:0], in_1[7]};
endmodule

module cmp1 (
  input  in_1,
  input  in_2,
  output out_3,
  output out_4,
  output out_5
);

  wire not_1_out, not_2_out, xor_1_out;

  not not_1 (not_1_out, in_1);
  not not_2 (not_2_out, in_2);
  and and_1 (out_3, not_1_out, in_2);
  xor xor_1 (xor_1_out, in_1, in_2);
  and and_2 (out_5, in_1, not_2_out);
  not not_3 (out_4, xor_1_out);
endmodule

module cmp2 (
  input  _0,
  input  _1,
  input  _0_2,
  input  _1_2,
  output out_5,
  output out_6,
  output out_7
);

  wire and_1_out, and_2_out, cmp1_1_out_3, cmp1_1_out_4, cmp1_1_out_5, cmp1_2_out_3, cmp1_2_out_4,
       cmp1_2_out_5;

  cmp1 cmp1_1 (.in_1(_0), .in_2(_0_2), .out_3(cmp1_1_out_3), .out_4(cmp1_1_out_4), .out_5(cmp1_1_out_5));
  cmp1 cmp1_2 (.in_1(_1), .in_2(_1_2), .out_3(cmp1_2_out_3), .out_4(cmp1_2_out_4), .out_5(cmp1_2_out_5));
  and and_1 (and_1_out, cmp1_1_out_5, cmp1_2_out_4);
  and and_2 (and_2_out, cmp1_1_out_3, cmp1_2_out_4);
  and and_3 (out_5, cmp1_1_out_4, cmp1_2_out_4);
  or or_1 (out_6, and_1_out, cmp1_2_out_5);
  or or_2 (out_7, and_2_out, cmp1_2_out_3);

  // Notes on the sheet:
  //   B
  //   A
endmodule

module MUX (
  input  in_1,
  input  in_2,
  input  in_3,
  input  in_4,
  input  [1:0] in_5,
  output out_6
);

  wire and_1_out, and_2_out, and_3_out, and_4_out, not_1_out, not_2_out, not_3_out, not_4_out;

  not not_1 (not_1_out, in_5[1]);
  not not_2 (not_2_out, in_5[0]);
  not not_3 (not_3_out, in_5[1]);
  not not_4 (not_4_out, in_5[0]);
  and and_1 (and_1_out, in_1, not_1_out, not_2_out);
  and and_2 (and_2_out, in_2, in_5[0], not_3_out);
  and and_3 (and_3_out, in_3, in_5[1], not_4_out);
  and and_4 (and_4_out, in_4, in_5[0], in_5[1]);
  or or_1 (out_6, and_1_out, and_2_out, and_3_out, and_4_out);
endmodule

module logic_shr (
  input  [2:0] in_1,
  input  [7:0] in_2,
  output [7:0] out_3
);

  wire multiplexer_1_out, multiplexer_2_out, multiplexer_3_out, multiplexer_4_out, multiplexer_5_out,
       multiplexer_6_out, multiplexer_7_out, multiplexer_8_out, multiplexer_9_out, multiplexer_10_out,
       multiplexer_11_out, multiplexer_12_out, multiplexer_13_out, multiplexer_14_out, multiplexer_15_out,
       multiplexer_16_out, not_1_out, not_2_out, not_3_out;

  not not_1 (not_1_out, in_1[2]);
  not not_2 (not_2_out, in_1[1]);
  not not_3 (not_3_out, in_1[0]);
  Multiplexer multiplexer_1 (.in0(1'b0), .in1(in_2[7]), .out(multiplexer_1_out), .sel(not_3_out));  // open: en
  Multiplexer multiplexer_2 (.in0(in_2[7]), .in1(in_2[6]), .out(multiplexer_2_out), .sel(not_3_out));  // open: en
  Multiplexer multiplexer_3 (.in0(in_2[6]), .in1(in_2[5]), .out(multiplexer_3_out), .sel(not_3_out));  // open: en
  Multiplexer multiplexer_4 (.in0(in_2[5]), .in1(in_2[4]), .out(multiplexer_4_out), .sel(not_3_out));  // open: en
  Multiplexer multiplexer_5 (.in0(in_2[4]), .in1(in_2[3]), .out(multiplexer_5_out), .sel(not_3_out));  // open: en
  Multiplexer multiplexer_6 (.in0(in_2[3]), .in1(in_2[2]), .out(multiplexer_6_out), .sel(not_3_out));  // open: en
  Multiplexer multiplexer_7 (.in0(in_2[2]), .in1(in_2[1]), .out(multiplexer_7_out), .sel(not_3_out));  // open: en
  Multiplexer multiplexer_8 (.in0(in_2[1]), .in1(in_2[0]), .out(multiplexer_8_out), .sel(not_3_out));  // open: en
  Multiplexer multiplexer_9 (
    .in0(1'b0), .in1(multiplexer_1_out), .out(multiplexer_9_out), .sel(not_2_out));  // open: en
  Multiplexer multiplexer_10 (
    .in0(1'b0), .in1(multiplexer_2_out), .out(multiplexer_10_out), .sel(not_2_out));  // open: en
  Multiplexer multiplexer_11 (
    .in0(multiplexer_1_out), .in1(multiplexer_3_out), .out(multiplexer_11_out), .sel(not_2_out));  // open: en
  Multiplexer multiplexer_12 (
    .in0(multiplexer_2_out), .in1(multiplexer_4_out), .out(multiplexer_12_out), .sel(not_2_out));  // open: en
  Multiplexer multiplexer_13 (
    .in0(multiplexer_3_out), .in1(multiplexer_5_out), .out(multiplexer_13_out), .sel(not_2_out));  // open: en
  Multiplexer multiplexer_14 (
    .in0(multiplexer_4_out), .in1(multiplexer_6_out), .out(multiplexer_14_out), .sel(not_2_out));  // open: en
  Multiplexer multiplexer_15 (
    .in0(multiplexer_5_out), .in1(multiplexer_7_out), .out(multiplexer_15_out), .sel(not_2_out));  // open: en
  Multiplexer multiplexer_16 (
    .in0(multiplexer_6_out), .in1(multiplexer_8_out), .out(multiplexer_16_out), .sel(not_2_out));  // open: en
  Multiplexer multiplexer_17 (.in0(1'b0), .in1(multiplexer_9_out), .out(out_3[7]), .sel(not_1_out));  // open: en
  Multiplexer multiplexer_18 (.in0(1'b0), .in1(multiplexer_10_out), .out(out_3[6]), .sel(not_1_out));  // open: en
  Multiplexer multiplexer_19 (.in0(1'b0), .in1(multiplexer_11_out), .out(out_3[5]), .sel(not_1_out));  // open: en
  Multiplexer multiplexer_20 (.in0(1'b0), .in1(multiplexer_12_out), .out(out_3[4]), .sel(not_1_out));  // open: en
  Multiplexer multiplexer_21 (
    .in0(multiplexer_9_out), .in1(multiplexer_13_out), .out(out_3[3]), .sel(not_1_out));  // open: en
  Multiplexer multiplexer_22 (
    .in0(multiplexer_10_out), .in1(multiplexer_14_out), .out(out_3[2]), .sel(not_1_out));  // open: en
  Multiplexer multiplexer_23 (
    .in0(multiplexer_11_out), .in1(multiplexer_15_out), .out(out_3[1]), .sel(not_1_out));  // open: en
  Multiplexer multiplexer_24 (
    .in0(multiplexer_12_out), .in1(multiplexer_16_out), .out(out_3[0]), .sel(not_1_out));  // open: en
endmodule

module logic_shl (
  input  [2:0] in_1,
  input  [7:0] in_2,
  output [7:0] out_3
);

  wire multiplexer_1_out, multiplexer_2_out, multiplexer_3_out, multiplexer_4_out, multiplexer_5_out,
       multiplexer_6_out, multiplexer_7_out, multiplexer_8_out, multiplexer_9_out, multiplexer_10_out,
       multiplexer_11_out, multiplexer_12_out, multiplexer_13_out, multiplexer_14_out, multiplexer_15_out,
       multiplexer_16_out, not_1_out, not_2_out, not_3_out;

  not not_1 (not_1_out, in_1[2]);
  not not_2 (not_2_out, in_1[1]);
  not not_3 (not_3_out, in_1[0]);
  Multiplexer multiplexer_1 (.in0(1'b0), .in1(in_2[0]), .out(multiplexer_1_out), .sel(not_3_out));  // open: en
  Multiplexer multiplexer_2 (.in0(in_2[0]), .in1(in_2[1]), .out(multiplexer_2_out), .sel(not_3_out));  // open: en
  Multiplexer multiplexer_3 (.in0(in_2[1]), .in1(in_2[2]), .out(multiplexer_3_out), .sel(not_3_out));  // open: en
  Multiplexer multiplexer_4 (.in0(in_2[2]), .in1(in_2[3]), .out(multiplexer_4_out), .sel(not_3_out));  // open: en
  Multiplexer multiplexer_5 (.in0(in_2[3]), .in1(in_2[4]), .out(multiplexer_5_out), .sel(not_3_out));  // open: en
  Multiplexer multiplexer_6 (.in0(in_2[4]), .in1(in_2[5]), .out(multiplexer_6_out), .sel(not_3_out));  // open: en
  Multiplexer multiplexer_7 (.in0(in_2[5]), .in1(in_2[6]), .out(multiplexer_7_out), .sel(not_3_out));  // open: en
  Multiplexer multiplexer_8 (.in0(in_2[6]), .in1(in_2[7]), .out(multiplexer_8_out), .sel(not_3_out));  // open: en
  Multiplexer multiplexer_9 (
    .in0(1'b0), .in1(multiplexer_1_out), .out(multiplexer_9_out), .sel(not_2_out));  // open: en
  Multiplexer multiplexer_10 (
    .in0(1'b0), .in1(multiplexer_2_out), .out(multiplexer_10_out), .sel(not_2_out));  // open: en
  Multiplexer multiplexer_11 (
    .in0(multiplexer_1_out), .in1(multiplexer_3_out), .out(multiplexer_11_out), .sel(not_2_out));  // open: en
  Multiplexer multiplexer_12 (
    .in0(multiplexer_2_out), .in1(multiplexer_4_out), .out(multiplexer_12_out), .sel(not_2_out));  // open: en
  Multiplexer multiplexer_13 (
    .in0(multiplexer_3_out), .in1(multiplexer_5_out), .out(multiplexer_13_out), .sel(not_2_out));  // open: en
  Multiplexer multiplexer_14 (
    .in0(multiplexer_4_out), .in1(multiplexer_6_out), .out(multiplexer_14_out), .sel(not_2_out));  // open: en
  Multiplexer multiplexer_15 (
    .in0(multiplexer_5_out), .in1(multiplexer_7_out), .out(multiplexer_15_out), .sel(not_2_out));  // open: en
  Multiplexer multiplexer_16 (
    .in0(multiplexer_6_out), .in1(multiplexer_8_out), .out(multiplexer_16_out), .sel(not_2_out));  // open: en
  Multiplexer multiplexer_17 (.in0(1'b0), .in1(multiplexer_9_out), .out(out_3[0]), .sel(not_1_out));  // open: en
  Multiplexer multiplexer_18 (.in0(1'b0), .in1(multiplexer_10_out), .out(out_3[1]), .sel(not_1_out));  // open: en
  Multiplexer multiplexer_19 (.in0(1'b0), .in1(multiplexer_11_out), .out(out_3[2]), .sel(not_1_out));  // open: en
  Multiplexer multiplexer_20 (.in0(1'b0), .in1(multiplexer_12_out), .out(out_3[3]), .sel(not_1_out));  // open: en
  Multiplexer multiplexer_21 (
    .in0(multiplexer_9_out), .in1(multiplexer_13_out), .out(out_3[4]), .sel(not_1_out));  // open: en
  Multiplexer multiplexer_22 (
    .in0(multiplexer_10_out), .in1(multiplexer_14_out), .out(out_3[5]), .sel(not_1_out));  // open: en
  Multiplexer multiplexer_23 (
    .in0(multiplexer_11_out), .in1(multiplexer_15_out), .out(out_3[6]), .sel(not_1_out));  // open: en
  Multiplexer multiplexer_24 (
    .in0(multiplexer_12_out), .in1(multiplexer_16_out), .out(out_3[7]), .sel(not_1_out));  // open: en
endmodule

module arifmetical_shr (
  input  [2:0] in_1,
  input  [7:0] in_2,
  output [7:0] out_3
);

  wire multiplexer_1_out, multiplexer_2_out, multiplexer_3_out, multiplexer_4_out, multiplexer_5_out,
       multiplexer_6_out, multiplexer_7_out, multiplexer_8_out, multiplexer_9_out, multiplexer_10_out,
       multiplexer_11_out, multiplexer_12_out, multiplexer_13_out, multiplexer_14_out, multiplexer_15_out,
       multiplexer_16_out, not_1_out, not_2_out, not_3_out;

  not not_1 (not_1_out, in_1[2]);
  not not_2 (not_2_out, in_1[1]);
  not not_3 (not_3_out, in_1[0]);
  Multiplexer multiplexer_1 (.in0(in_2[7]), .in1(in_2[7]), .out(multiplexer_1_out), .sel(not_3_out));  // open: en
  Multiplexer multiplexer_2 (.in0(in_2[7]), .in1(in_2[6]), .out(multiplexer_2_out), .sel(not_3_out));  // open: en
  Multiplexer multiplexer_3 (.in0(in_2[6]), .in1(in_2[5]), .out(multiplexer_3_out), .sel(not_3_out));  // open: en
  Multiplexer multiplexer_4 (.in0(in_2[5]), .in1(in_2[4]), .out(multiplexer_4_out), .sel(not_3_out));  // open: en
  Multiplexer multiplexer_5 (.in0(in_2[4]), .in1(in_2[3]), .out(multiplexer_5_out), .sel(not_3_out));  // open: en
  Multiplexer multiplexer_6 (.in0(in_2[3]), .in1(in_2[2]), .out(multiplexer_6_out), .sel(not_3_out));  // open: en
  Multiplexer multiplexer_7 (.in0(in_2[2]), .in1(in_2[1]), .out(multiplexer_7_out), .sel(not_3_out));  // open: en
  Multiplexer multiplexer_8 (.in0(in_2[1]), .in1(in_2[0]), .out(multiplexer_8_out), .sel(not_3_out));  // open: en
  Multiplexer multiplexer_9 (
    .in0(in_2[7]), .in1(multiplexer_1_out), .out(multiplexer_9_out), .sel(not_2_out));  // open: en
  Multiplexer multiplexer_10 (
    .in0(in_2[7]), .in1(multiplexer_2_out), .out(multiplexer_10_out), .sel(not_2_out));  // open: en
  Multiplexer multiplexer_11 (
    .in0(multiplexer_1_out), .in1(multiplexer_3_out), .out(multiplexer_11_out), .sel(not_2_out));  // open: en
  Multiplexer multiplexer_12 (
    .in0(multiplexer_2_out), .in1(multiplexer_4_out), .out(multiplexer_12_out), .sel(not_2_out));  // open: en
  Multiplexer multiplexer_13 (
    .in0(multiplexer_3_out), .in1(multiplexer_5_out), .out(multiplexer_13_out), .sel(not_2_out));  // open: en
  Multiplexer multiplexer_14 (
    .in0(multiplexer_4_out), .in1(multiplexer_6_out), .out(multiplexer_14_out), .sel(not_2_out));  // open: en
  Multiplexer multiplexer_15 (
    .in0(multiplexer_5_out), .in1(multiplexer_7_out), .out(multiplexer_15_out), .sel(not_2_out));  // open: en
  Multiplexer multiplexer_16 (
    .in0(multiplexer_6_out), .in1(multiplexer_8_out), .out(multiplexer_16_out), .sel(not_2_out));  // open: en
  Multiplexer multiplexer_17 (.in0(in_2[7]), .in1(multiplexer_9_out), .out(out_3[7]), .sel(not_1_out));  // open: en
  Multiplexer multiplexer_18 (.in0(in_2[7]), .in1(multiplexer_10_out), .out(out_3[6]), .sel(not_1_out));  // open: en
  Multiplexer multiplexer_19 (.in0(in_2[7]), .in1(multiplexer_11_out), .out(out_3[5]), .sel(not_1_out));  // open: en
  Multiplexer multiplexer_20 (.in0(in_2[7]), .in1(multiplexer_12_out), .out(out_3[4]), .sel(not_1_out));  // open: en
  Multiplexer multiplexer_21 (
    .in0(multiplexer_9_out), .in1(multiplexer_13_out), .out(out_3[3]), .sel(not_1_out));  // open: en
  Multiplexer multiplexer_22 (
    .in0(multiplexer_10_out), .in1(multiplexer_14_out), .out(out_3[2]), .sel(not_1_out));  // open: en
  Multiplexer multiplexer_23 (
    .in0(multiplexer_11_out), .in1(multiplexer_15_out), .out(out_3[1]), .sel(not_1_out));  // open: en
  Multiplexer multiplexer_24 (
    .in0(multiplexer_12_out), .in1(multiplexer_16_out), .out(out_3[0]), .sel(not_1_out));  // open: en
endmodule

module arifmetical_shl (
  input  [2:0] in_1,
  input  [7:0] in_2,
  output [7:0] out_3
);

  wire multiplexer_1_out, multiplexer_2_out, multiplexer_3_out, multiplexer_4_out, multiplexer_5_out,
       multiplexer_6_out, multiplexer_7_out, multiplexer_8_out, multiplexer_9_out, multiplexer_10_out,
       multiplexer_11_out, multiplexer_12_out, multiplexer_13_out, multiplexer_14_out, multiplexer_15_out,
       multiplexer_16_out, not_1_out, not_2_out, not_3_out;

  not not_1 (not_1_out, in_1[2]);
  not not_2 (not_2_out, in_1[1]);
  not not_3 (not_3_out, in_1[0]);
  Multiplexer multiplexer_1 (.in0(in_2[0]), .in1(in_2[0]), .out(multiplexer_1_out), .sel(not_3_out));  // open: en
  Multiplexer multiplexer_2 (.in0(in_2[0]), .in1(in_2[1]), .out(multiplexer_2_out), .sel(not_3_out));  // open: en
  Multiplexer multiplexer_3 (.in0(in_2[1]), .in1(in_2[2]), .out(multiplexer_3_out), .sel(not_3_out));  // open: en
  Multiplexer multiplexer_4 (.in0(in_2[2]), .in1(in_2[3]), .out(multiplexer_4_out), .sel(not_3_out));  // open: en
  Multiplexer multiplexer_5 (.in0(in_2[3]), .in1(in_2[4]), .out(multiplexer_5_out), .sel(not_3_out));  // open: en
  Multiplexer multiplexer_6 (.in0(in_2[4]), .in1(in_2[5]), .out(multiplexer_6_out), .sel(not_3_out));  // open: en
  Multiplexer multiplexer_7 (.in0(in_2[5]), .in1(in_2[6]), .out(multiplexer_7_out), .sel(not_3_out));  // open: en
  Multiplexer multiplexer_8 (.in0(in_2[6]), .in1(in_2[7]), .out(multiplexer_8_out), .sel(not_3_out));  // open: en
  Multiplexer multiplexer_9 (
    .in0(in_2[0]), .in1(multiplexer_1_out), .out(multiplexer_9_out), .sel(not_2_out));  // open: en
  Multiplexer multiplexer_10 (
    .in0(in_2[0]), .in1(multiplexer_2_out), .out(multiplexer_10_out), .sel(not_2_out));  // open: en
  Multiplexer multiplexer_11 (
    .in0(multiplexer_1_out), .in1(multiplexer_3_out), .out(multiplexer_11_out), .sel(not_2_out));  // open: en
  Multiplexer multiplexer_12 (
    .in0(multiplexer_2_out), .in1(multiplexer_4_out), .out(multiplexer_12_out), .sel(not_2_out));  // open: en
  Multiplexer multiplexer_13 (
    .in0(multiplexer_3_out), .in1(multiplexer_5_out), .out(multiplexer_13_out), .sel(not_2_out));  // open: en
  Multiplexer multiplexer_14 (
    .in0(multiplexer_4_out), .in1(multiplexer_6_out), .out(multiplexer_14_out), .sel(not_2_out));  // open: en
  Multiplexer multiplexer_15 (
    .in0(multiplexer_5_out), .in1(multiplexer_7_out), .out(multiplexer_15_out), .sel(not_2_out));  // open: en
  Multiplexer multiplexer_16 (
    .in0(multiplexer_6_out), .in1(multiplexer_8_out), .out(multiplexer_16_out), .sel(not_2_out));  // open: en
  Multiplexer multiplexer_17 (.in0(in_2[0]), .in1(multiplexer_9_out), .out(out_3[0]), .sel(not_1_out));  // open: en
  Multiplexer multiplexer_18 (.in0(in_2[0]), .in1(multiplexer_10_out), .out(out_3[1]), .sel(not_1_out));  // open: en
  Multiplexer multiplexer_19 (.in0(in_2[0]), .in1(multiplexer_11_out), .out(out_3[2]), .sel(not_1_out));  // open: en
  Multiplexer multiplexer_20 (.in0(in_2[0]), .in1(multiplexer_12_out), .out(out_3[3]), .sel(not_1_out));  // open: en
  Multiplexer multiplexer_21 (
    .in0(multiplexer_9_out), .in1(multiplexer_13_out), .out(out_3[4]), .sel(not_1_out));  // open: en
  Multiplexer multiplexer_22 (
    .in0(multiplexer_10_out), .in1(multiplexer_14_out), .out(out_3[5]), .sel(not_1_out));  // open: en
  Multiplexer multiplexer_23 (
    .in0(multiplexer_11_out), .in1(multiplexer_15_out), .out(out_3[6]), .sel(not_1_out));  // open: en
  Multiplexer multiplexer_24 (
    .in0(multiplexer_12_out), .in1(multiplexer_16_out), .out(out_3[7]), .sel(not_1_out));  // open: en
endmodule

module cycle_shr (
  input  [2:0] in_1,
  input  [7:0] in_2,
  output [7:0] out_3
);

  wire multiplexer_1_out, multiplexer_2_out, multiplexer_3_out, multiplexer_4_out, multiplexer_5_out,
       multiplexer_6_out, multiplexer_7_out, multiplexer_8_out, multiplexer_9_out, multiplexer_10_out,
       multiplexer_11_out, multiplexer_12_out, multiplexer_13_out, multiplexer_14_out, multiplexer_15_out,
       multiplexer_16_out;

  Multiplexer multiplexer_1 (.in0(in_2[7]), .in1(in_2[0]), .out(multiplexer_1_out), .sel(in_1[0]));  // open: en
  Multiplexer multiplexer_2 (.in0(in_2[0]), .in1(in_2[1]), .out(multiplexer_2_out), .sel(in_1[0]));  // open: en
  Multiplexer multiplexer_3 (.in0(in_2[1]), .in1(in_2[2]), .out(multiplexer_3_out), .sel(in_1[0]));  // open: en
  Multiplexer multiplexer_4 (.in0(in_2[2]), .in1(in_2[3]), .out(multiplexer_4_out), .sel(in_1[0]));  // open: en
  Multiplexer multiplexer_5 (.in0(in_2[3]), .in1(in_2[4]), .out(multiplexer_5_out), .sel(in_1[0]));  // open: en
  Multiplexer multiplexer_6 (.in0(in_2[4]), .in1(in_2[5]), .out(multiplexer_6_out), .sel(in_1[0]));  // open: en
  Multiplexer multiplexer_7 (.in0(in_2[5]), .in1(in_2[6]), .out(multiplexer_7_out), .sel(in_1[0]));  // open: en
  Multiplexer multiplexer_8 (.in0(in_2[6]), .in1(in_2[7]), .out(multiplexer_8_out), .sel(in_1[0]));  // open: en
  Multiplexer multiplexer_9 (
    .in0(multiplexer_7_out), .in1(multiplexer_1_out), .out(multiplexer_9_out), .sel(in_1[1]));  // open: en
  Multiplexer multiplexer_10 (
    .in0(multiplexer_8_out), .in1(multiplexer_2_out), .out(multiplexer_10_out), .sel(in_1[1]));  // open: en
  Multiplexer multiplexer_11 (
    .in0(multiplexer_1_out), .in1(multiplexer_3_out), .out(multiplexer_11_out), .sel(in_1[1]));  // open: en
  Multiplexer multiplexer_12 (
    .in0(multiplexer_2_out), .in1(multiplexer_4_out), .out(multiplexer_12_out), .sel(in_1[1]));  // open: en
  Multiplexer multiplexer_13 (
    .in0(multiplexer_3_out), .in1(multiplexer_5_out), .out(multiplexer_13_out), .sel(in_1[1]));  // open: en
  Multiplexer multiplexer_14 (
    .in0(multiplexer_4_out), .in1(multiplexer_6_out), .out(multiplexer_14_out), .sel(in_1[1]));  // open: en
  Multiplexer multiplexer_15 (
    .in0(multiplexer_5_out), .in1(multiplexer_7_out), .out(multiplexer_15_out), .sel(in_1[1]));  // open: en
  Multiplexer multiplexer_16 (
    .in0(multiplexer_6_out), .in1(multiplexer_8_out), .out(multiplexer_16_out), .sel(in_1[1]));  // open: en
  Multiplexer multiplexer_17 (
    .in0(multiplexer_13_out), .in1(multiplexer_9_out), .out(out_3[0]), .sel(in_1[2]));  // open: en
  Multiplexer multiplexer_18 (
    .in0(multiplexer_14_out), .in1(multiplexer_10_out), .out(out_3[1]), .sel(in_1[2]));  // open: en
  Multiplexer multiplexer_19 (
    .in0(multiplexer_15_out), .in1(multiplexer_11_out), .out(out_3[2]), .sel(in_1[2]));  // open: en
  Multiplexer multiplexer_20 (
    .in0(multiplexer_16_out), .in1(multiplexer_12_out), .out(out_3[3]), .sel(in_1[2]));  // open: en
  Multiplexer multiplexer_21 (
    .in0(multiplexer_9_out), .in1(multiplexer_13_out), .out(out_3[4]), .sel(in_1[2]));  // open: en
  Multiplexer multiplexer_22 (
    .in0(multiplexer_10_out), .in1(multiplexer_14_out), .out(out_3[5]), .sel(in_1[2]));  // open: en
  Multiplexer multiplexer_23 (
    .in0(multiplexer_11_out), .in1(multiplexer_15_out), .out(out_3[6]), .sel(in_1[2]));  // open: en
  Multiplexer multiplexer_24 (
    .in0(multiplexer_12_out), .in1(multiplexer_16_out), .out(out_3[7]), .sel(in_1[2]));  // open: en
endmodule

module cycle_shl (
  input  [2:0] in_1,
  input  [7:0] in_2,
  output [7:0] out_3
);

  wire multiplexer_1_out, multiplexer_2_out, multiplexer_3_out, multiplexer_4_out, multiplexer_5_out,
       multiplexer_6_out, multiplexer_7_out, multiplexer_8_out, multiplexer_9_out, multiplexer_10_out,
       multiplexer_11_out, multiplexer_12_out, multiplexer_13_out, multiplexer_14_out, multiplexer_15_out,
       multiplexer_16_out;

  Multiplexer multiplexer_1 (.in0(in_2[0]), .in1(in_2[7]), .out(multiplexer_1_out), .sel(in_1[0]));  // open: en
  Multiplexer multiplexer_2 (.in0(in_2[7]), .in1(in_2[6]), .out(multiplexer_2_out), .sel(in_1[0]));  // open: en
  Multiplexer multiplexer_3 (.in0(in_2[6]), .in1(in_2[5]), .out(multiplexer_3_out), .sel(in_1[0]));  // open: en
  Multiplexer multiplexer_4 (.in0(in_2[5]), .in1(in_2[4]), .out(multiplexer_4_out), .sel(in_1[0]));  // open: en
  Multiplexer multiplexer_5 (.in0(in_2[4]), .in1(in_2[3]), .out(multiplexer_5_out), .sel(in_1[0]));  // open: en
  Multiplexer multiplexer_6 (.in0(in_2[3]), .in1(in_2[2]), .out(multiplexer_6_out), .sel(in_1[0]));  // open: en
  Multiplexer multiplexer_7 (.in0(in_2[2]), .in1(in_2[1]), .out(multiplexer_7_out), .sel(in_1[0]));  // open: en
  Multiplexer multiplexer_8 (.in0(in_2[1]), .in1(in_2[0]), .out(multiplexer_8_out), .sel(in_1[0]));  // open: en
  Multiplexer multiplexer_9 (
    .in0(multiplexer_7_out), .in1(multiplexer_1_out), .out(multiplexer_9_out), .sel(in_1[1]));  // open: en
  Multiplexer multiplexer_10 (
    .in0(multiplexer_8_out), .in1(multiplexer_2_out), .out(multiplexer_10_out), .sel(in_1[1]));  // open: en
  Multiplexer multiplexer_11 (
    .in0(multiplexer_1_out), .in1(multiplexer_3_out), .out(multiplexer_11_out), .sel(in_1[1]));  // open: en
  Multiplexer multiplexer_12 (
    .in0(multiplexer_2_out), .in1(multiplexer_4_out), .out(multiplexer_12_out), .sel(in_1[1]));  // open: en
  Multiplexer multiplexer_13 (
    .in0(multiplexer_3_out), .in1(multiplexer_5_out), .out(multiplexer_13_out), .sel(in_1[1]));  // open: en
  Multiplexer multiplexer_14 (
    .in0(multiplexer_4_out), .in1(multiplexer_6_out), .out(multiplexer_14_out), .sel(in_1[1]));  // open: en
  Multiplexer multiplexer_15 (
    .in0(multiplexer_5_out), .in1(multiplexer_7_out), .out(multiplexer_15_out), .sel(in_1[1]));  // open: en
  Multiplexer multiplexer_16 (
    .in0(multiplexer_6_out), .in1(multiplexer_8_out), .out(multiplexer_16_out), .sel(in_1[1]));  // open: en
  Multiplexer multiplexer_17 (
    .in0(multiplexer_13_out), .in1(multiplexer_9_out), .out(out_3[0]), .sel(in_1[2]));  // open: en
  Multiplexer multiplexer_18 (
    .in0(multiplexer_14_out), .in1(multiplexer_10_out), .out(out_3[7]), .sel(in_1[2]));  // open: en
  Multiplexer multiplexer_19 (
    .in0(multiplexer_15_out), .in1(multiplexer_11_out), .out(out_3[6]), .sel(in_1[2]));  // open: en
  Multiplexer multiplexer_20 (
    .in0(multiplexer_16_out), .in1(multiplexer_12_out), .out(out_3[5]), .sel(in_1[2]));  // open: en
  Multiplexer multiplexer_21 (
    .in0(multiplexer_9_out), .in1(multiplexer_13_out), .out(out_3[4]), .sel(in_1[2]));  // open: en
  Multiplexer multiplexer_22 (
    .in0(multiplexer_10_out), .in1(multiplexer_14_out), .out(out_3[3]), .sel(in_1[2]));  // open: en
  Multiplexer multiplexer_23 (
    .in0(multiplexer_11_out), .in1(multiplexer_15_out), .out(out_3[2]), .sel(in_1[2]));  // open: en
  Multiplexer multiplexer_24 (
    .in0(multiplexer_12_out), .in1(multiplexer_16_out), .out(out_3[1]), .sel(in_1[2]));  // open: en
endmodule

module less_1_bit (
  input  in_1,
  input  in_2,
  output out_3
);

  wire not_1_out;

  not not_1 (not_1_out, in_1);
  and and_1 (out_3, not_1_out, in_2);
endmodule

module not_more_1_bit (
  input  in_1,
  input  in_2,
  output out_3
);

  wire not_1_out;

  not not_1 (not_1_out, in_2);
  nand nand_1 (out_3, in_1, not_1_out);
endmodule

module less_8_bit_no_sign (
  input  [7:0] in_1,
  input  [7:0] in_2,
  output out_3
);

  wire and_1_out, and_2_out, and_3_out, and_4_out, and_5_out, and_6_out, and_7_out, less_1_bit_1_out_3,
       less_1_bit_2_out_3, less_1_bit_3_out_3, less_1_bit_4_out_3, less_1_bit_5_out_3, less_1_bit_6_out_3,
       less_1_bit_7_out_3, less_1_bit_8_out_3, not_more_1_bit_1_out_3, not_more_1_bit_2_out_3,
       not_more_1_bit_3_out_3, not_more_1_bit_4_out_3, not_more_1_bit_5_out_3, not_more_1_bit_6_out_3,
       not_more_1_bit_7_out_3;

  less_1_bit less_1_bit_1 (.in_1(in_1[7]), .in_2(in_2[7]), .out_3(less_1_bit_1_out_3));
  less_1_bit less_1_bit_2 (.in_1(in_1[6]), .in_2(in_2[6]), .out_3(less_1_bit_2_out_3));
  less_1_bit less_1_bit_3 (.in_1(in_1[5]), .in_2(in_2[5]), .out_3(less_1_bit_3_out_3));
  not_more_1_bit not_more_1_bit_1 (.in_1(in_1[7]), .in_2(in_2[7]), .out_3(not_more_1_bit_1_out_3));
  not_more_1_bit not_more_1_bit_2 (.in_1(in_1[6]), .in_2(in_2[6]), .out_3(not_more_1_bit_2_out_3));
  not_more_1_bit not_more_1_bit_3 (.in_1(in_1[5]), .in_2(in_2[5]), .out_3(not_more_1_bit_3_out_3));
  less_1_bit less_1_bit_4 (.in_1(in_1[4]), .in_2(in_2[4]), .out_3(less_1_bit_4_out_3));
  not_more_1_bit not_more_1_bit_4 (.in_1(in_1[4]), .in_2(in_2[4]), .out_3(not_more_1_bit_4_out_3));
  less_1_bit less_1_bit_5 (.in_1(in_1[3]), .in_2(in_2[3]), .out_3(less_1_bit_5_out_3));
  not_more_1_bit not_more_1_bit_5 (.in_1(in_1[3]), .in_2(in_2[3]), .out_3(not_more_1_bit_5_out_3));
  less_1_bit less_1_bit_6 (.in_1(in_1[2]), .in_2(in_2[2]), .out_3(less_1_bit_6_out_3));
  not_more_1_bit not_more_1_bit_6 (.in_1(in_1[2]), .in_2(in_2[2]), .out_3(not_more_1_bit_6_out_3));
  less_1_bit less_1_bit_7 (.in_1(in_1[1]), .in_2(in_2[1]), .out_3(less_1_bit_7_out_3));
  not_more_1_bit not_more_1_bit_7 (.in_1(in_1[1]), .in_2(in_2[1]), .out_3(not_more_1_bit_7_out_3));
  less_1_bit less_1_bit_8 (.in_1(in_1[0]), .in_2(in_2[0]), .out_3(less_1_bit_8_out_3));
  and and_1 (and_1_out, not_more_1_bit_1_out_3, less_1_bit_2_out_3);
  and and_2 (and_2_out, not_more_1_bit_1_out_3, not_more_1_bit_2_out_3, less_1_bit_3_out_3);
  and and_3 (and_3_out, not_more_1_bit_1_out_3, not_more_1_bit_2_out_3, not_more_1_bit_3_out_3, less_1_bit_4_out_3);
  and and_4 (and_4_out, not_more_1_bit_1_out_3, not_more_1_bit_2_out_3, not_more_1_bit_3_out_3, not_more_1_bit_4_out_3, less_1_bit_5_out_3);
  and and_5 (and_5_out, not_more_1_bit_1_out_3, not_more_1_bit_2_out_3, not_more_1_bit_3_out_3, not_more_1_bit_4_out_3, not_more_1_bit_5_out_3, less_1_bit_6_out_3);
  and and_6 (and_6_out, not_more_1_bit_1_out_3, not_more_1_bit_2_out_3, not_more_1_bit_3_out_3, not_more_1_bit_4_out_3, not_more_1_bit_5_out_3, not_more_1_bit_6_out_3, less_1_bit_7_out_3);
  and and_7 (and_7_out, not_more_1_bit_1_out_3, not_more_1_bit_2_out_3, not_more_1_bit_3_out_3, not_more_1_bit_4_out_3, not_more_1_bit_5_out_3, not_more_1_bit_6_out_3, not_more_1_bit_7_out_3, less_1_bit_8_out_3);
  or or_1 (out_3, less_1_bit_1_out_3, and_1_out, and_2_out, and_3_out, and_4_out, and_5_out, and_6_out, and_7_out);
endmodule

module bigger_8_bit_no_sign (
  input  [7:0] in_1,
  input  [7:0] in_2,
  output out_3
);

  less_8_bit_no_sign less_8_bit_no_sign_1 (.in_1(in_2), .in_2(in_1), .out_3(out_3));
endmodule

module equal_8_bit_no_sign (
  input  [7:0] in_1,
  input  [7:0] in_2,
  output out_3
);

  wire bigger_8_bit_no_sign_1_out_3, less_8_bit_no_sign_1_out_3, not_1_out, not_2_out;

  less_8_bit_no_sign less_8_bit_no_sign_1 (.in_1(in_1), .in_2(in_2), .out_3(less_8_bit_no_sign_1_out_3));
  not not_1 (not_1_out, less_8_bit_no_sign_1_out_3);
  bigger_8_bit_no_sign bigger_8_bit_no_sign_1 (.in_1(in_1), .in_2(in_2), .out_3(bigger_8_bit_no_sign_1_out_3));
  not not_2 (not_2_out, bigger_8_bit_no_sign_1_out_3);
  and and_1 (out_3, not_1_out, not_2_out);
endmodule

module less_or_equal_8_bit_no_sign (
  input  [7:0] in_1,
  input  [7:0] in_2,
  output out_3
);

  wire equal_8_bit_no_sign_1_out_3, less_8_bit_no_sign_1_out_3;

  less_8_bit_no_sign less_8_bit_no_sign_1 (.in_1(in_1), .in_2(in_2), .out_3(less_8_bit_no_sign_1_out_3));
  equal_8_bit_no_sign equal_8_bit_no_sign_1 (.in_1(in_1), .in_2(in_2), .out_3(equal_8_bit_no_sign_1_out_3));
  or or_1 (out_3, less_8_bit_no_sign_1_out_3, equal_8_bit_no_sign_1_out_3);
endmodule

module bigger_or_equal_8_bit_no_sign (
  input  [7:0] in_1,
  input  [7:0] in_2,
  output out_3
);

  wire bigger_8_bit_no_sign_1_out_3, equal_8_bit_no_sign_1_out_3;

  bigger_8_bit_no_sign bigger_8_bit_no_sign_1 (.in_1(in_1), .in_2(in_2), .out_3(bigger_8_bit_no_sign_1_out_3));
  equal_8_bit_no_sign equal_8_bit_no_sign_1 (.in_1(in_1), .in_2(in_2), .out_3(equal_8_bit_no_sign_1_out_3));
  or or_1 (out_3, bigger_8_bit_no_sign_1_out_3, equal_8_bit_no_sign_1_out_3);
endmodule

module not_equal_8_bit_no_sign (
  input  [7:0] in_1,
  input  [7:0] in_2,
  output out_3
);

  wire and_1_out, bigger_8_bit_no_sign_1_out_3, less_8_bit_no_sign_1_out_3, not_1_out, not_2_out;

  less_8_bit_no_sign less_8_bit_no_sign_1 (.in_1(in_1), .in_2(in_2), .out_3(less_8_bit_no_sign_1_out_3));
  not not_1 (not_1_out, less_8_bit_no_sign_1_out_3);
  not not_2 (not_2_out, bigger_8_bit_no_sign_1_out_3);
  bigger_8_bit_no_sign bigger_8_bit_no_sign_1 (.in_1(in_1), .in_2(in_2), .out_3(bigger_8_bit_no_sign_1_out_3));
  and and_1 (and_1_out, not_1_out, not_2_out);
  not not_3 (out_3, and_1_out);
endmodule

module less_7_bit_nosign (
  input  [6:0] in_1,
  input  [6:0] in_2,
  output out_3
);

  wire and_1_out, and_2_out, and_3_out, and_4_out, and_5_out, and_6_out, less_1_bit_1_out_3,
       less_1_bit_2_out_3, less_1_bit_3_out_3, less_1_bit_4_out_3, less_1_bit_5_out_3, less_1_bit_6_out_3,
       less_1_bit_7_out_3, not_more_1_bit_1_out_3, not_more_1_bit_2_out_3, not_more_1_bit_3_out_3,
       not_more_1_bit_4_out_3, not_more_1_bit_5_out_3, not_more_1_bit_6_out_3;

  less_1_bit less_1_bit_1 (.in_1(in_1[6]), .in_2(in_2[6]), .out_3(less_1_bit_1_out_3));
  less_1_bit less_1_bit_2 (.in_1(in_1[5]), .in_2(in_2[5]), .out_3(less_1_bit_2_out_3));
  less_1_bit less_1_bit_3 (.in_1(in_1[4]), .in_2(in_2[4]), .out_3(less_1_bit_3_out_3));
  not_more_1_bit not_more_1_bit_1 (.in_1(in_1[6]), .in_2(in_2[6]), .out_3(not_more_1_bit_1_out_3));
  not_more_1_bit not_more_1_bit_2 (.in_1(in_1[5]), .in_2(in_2[5]), .out_3(not_more_1_bit_2_out_3));
  not_more_1_bit not_more_1_bit_3 (.in_1(in_1[4]), .in_2(in_2[4]), .out_3(not_more_1_bit_3_out_3));
  less_1_bit less_1_bit_4 (.in_1(in_1[3]), .in_2(in_2[3]), .out_3(less_1_bit_4_out_3));
  not_more_1_bit not_more_1_bit_4 (.in_1(in_1[3]), .in_2(in_2[3]), .out_3(not_more_1_bit_4_out_3));
  less_1_bit less_1_bit_5 (.in_1(in_1[2]), .in_2(in_2[2]), .out_3(less_1_bit_5_out_3));
  not_more_1_bit not_more_1_bit_5 (.in_1(in_1[2]), .in_2(in_2[2]), .out_3(not_more_1_bit_5_out_3));
  less_1_bit less_1_bit_6 (.in_1(in_1[1]), .in_2(in_2[1]), .out_3(less_1_bit_6_out_3));
  not_more_1_bit not_more_1_bit_6 (.in_1(in_1[1]), .in_2(in_2[1]), .out_3(not_more_1_bit_6_out_3));
  less_1_bit less_1_bit_7 (.in_1(in_1[0]), .in_2(in_2[0]), .out_3(less_1_bit_7_out_3));
  and and_1 (and_1_out, not_more_1_bit_1_out_3, less_1_bit_2_out_3);
  and and_2 (and_2_out, not_more_1_bit_1_out_3, not_more_1_bit_2_out_3, less_1_bit_3_out_3);
  and and_3 (and_3_out, not_more_1_bit_1_out_3, not_more_1_bit_2_out_3, not_more_1_bit_3_out_3, less_1_bit_4_out_3);
  and and_4 (and_4_out, not_more_1_bit_1_out_3, not_more_1_bit_2_out_3, not_more_1_bit_3_out_3, not_more_1_bit_4_out_3, less_1_bit_5_out_3);
  and and_5 (and_5_out, not_more_1_bit_1_out_3, not_more_1_bit_2_out_3, not_more_1_bit_3_out_3, not_more_1_bit_4_out_3, not_more_1_bit_5_out_3, less_1_bit_6_out_3);
  and and_6 (and_6_out, not_more_1_bit_1_out_3, not_more_1_bit_2_out_3, not_more_1_bit_3_out_3, not_more_1_bit_4_out_3, not_more_1_bit_5_out_3, not_more_1_bit_6_out_3, less_1_bit_7_out_3);
  or or_1 (out_3, less_1_bit_1_out_3, and_1_out, and_2_out, and_3_out, and_4_out, and_5_out, and_6_out);
endmodule

module bigger_7_bit_no_sign (
  input  [6:0] in_1,
  input  [6:0] in_2,
  output out_3
);

  less_7_bit_nosign less_7_bit_nosign_1 (.in_1(in_2), .in_2(in_1), .out_3(out_3));
endmodule

module less_8__bit_sign (
  input  [7:0] in_1,
  input  [7:0] in_2,
  output out_3
);

  wire and_1_out, and_2_out, and_3_out, bigger_7_bit_no_sign_1_out_3, less_7_bit_nosign_1_out_3, not_1_out,
       not_2_out, not_3_out, not_4_out;

  not not_1 (not_1_out, in_2[7]);
  less_7_bit_nosign less_7_bit_nosign_1 (.in_1(in_1[6:0]), .in_2(in_2[6:0]), .out_3(less_7_bit_nosign_1_out_3));
  bigger_7_bit_no_sign bigger_7_bit_no_sign_1 (
    .in_1(in_1[6:0]), .in_2(in_2[6:0]), .out_3(bigger_7_bit_no_sign_1_out_3));
  not not_2 (not_2_out, bigger_7_bit_no_sign_1_out_3);
  and and_1 (and_1_out, in_1[7], not_3_out, bigger_7_bit_no_sign_1_out_3);
  not not_3 (not_3_out, less_7_bit_nosign_1_out_3);
  and and_2 (and_2_out, in_1[7], not_1_out, not_4_out);
  not not_4 (not_4_out, bigger_7_bit_no_sign_1_out_3);
  and and_3 (and_3_out, less_7_bit_nosign_1_out_3, not_2_out, not_1_out);
  or or_1 (out_3, and_1_out, and_2_out, and_3_out);
endmodule

module bigger_8_bit_sign (
  input  [7:0] in_1,
  input  [7:0] in_2,
  output out_3
);

  less_8__bit_sign less_8_bit_sign_1 (.in_1(in_2), .in_2(in_1), .out_3(out_3));
endmodule

module equal_8_bit_sign (
  input  [7:0] in_1,
  input  [7:0] in_2,
  output out_3
);

  wire bigger_8_bit_sign_1_out_3, less_8_bit_sign_1_out_3, not_1_out, not_2_out;

  not not_1 (not_1_out, less_8_bit_sign_1_out_3);
  less_8__bit_sign less_8_bit_sign_1 (.in_1(in_1), .in_2(in_2), .out_3(less_8_bit_sign_1_out_3));
  bigger_8_bit_sign bigger_8_bit_sign_1 (.in_1(in_1), .in_2(in_2), .out_3(bigger_8_bit_sign_1_out_3));
  not not_2 (not_2_out, bigger_8_bit_sign_1_out_3);
  and and_1 (out_3, not_1_out, not_2_out);
endmodule

module less_or_equal_8_bit_sign (
  input  [7:0] in_1,
  input  [7:0] in_2,
  output out_3
);

  wire equal_8_bit_sign_1_out_3, less_8_bit_sign_1_out_3;

  less_8__bit_sign less_8_bit_sign_1 (.in_1(in_1), .in_2(in_2), .out_3(less_8_bit_sign_1_out_3));
  equal_8_bit_sign equal_8_bit_sign_1 (.in_1(in_1), .in_2(in_2), .out_3(equal_8_bit_sign_1_out_3));
  or or_1 (out_3, less_8_bit_sign_1_out_3, equal_8_bit_sign_1_out_3);
endmodule

module bigger_or_equal_8_bit_sign (
  input  [7:0] in_1,
  input  [7:0] in_2,
  output out_3
);

  wire bigger_8_bit_sign_1_out_3, equal_8_bit_sign_1_out_3;

  bigger_8_bit_sign bigger_8_bit_sign_1 (.in_1(in_1), .in_2(in_2), .out_3(bigger_8_bit_sign_1_out_3));
  equal_8_bit_sign equal_8_bit_sign_1 (.in_1(in_1), .in_2(in_2), .out_3(equal_8_bit_sign_1_out_3));
  or or_1 (out_3, bigger_8_bit_sign_1_out_3, equal_8_bit_sign_1_out_3);
endmodule

module half_substracter (
  input  in_1,
  input  in_2,
  output out_3,
  output out_4
);

  wire not_1_out;

  not not_1 (not_1_out, in_1);
  xor xor_1 (out_3, in_1, in_2);
  and and_1 (out_4, not_1_out, in_2);
endmodule

module substracter (
  input  in_1,
  input  in_2,
  input  in_3,
  output out_4,
  output out_5
);

  wire half_substracter_1_out_3, half_substracter_1_out_4, half_substracter_2_out_4;

  half_substracter half_substracter_1 (
    .in_1(in_1), .in_2(in_2), .out_3(half_substracter_1_out_3), .out_4(half_substracter_1_out_4));
  half_substracter half_substracter_2 (
    .in_1(half_substracter_1_out_3), .in_2(in_3), .out_3(out_4), .out_4(half_substracter_2_out_4));
  or or_1 (out_5, half_substracter_2_out_4, half_substracter_1_out_4);
endmodule

module substracter_8_bit (
  input  [7:0] in_1,
  input  [7:0] in_2,
  output [7:0] out_3,
  output out_4
);

  wire substracter_1_out_5, substracter_2_out_5, substracter_3_out_5, substracter_4_out_5,
       substracter_5_out_5, substracter_6_out_5, substracter_7_out_5;

  substracter substracter_1 (
    .in_1(in_1[0]), .in_2(in_2[0]), .in_3(1'b0), .out_4(out_3[0]), .out_5(substracter_1_out_5));
  substracter substracter_2 (
    .in_1(in_1[1]), .in_2(in_2[1]), .in_3(substracter_1_out_5), .out_4(out_3[1]), .out_5(substracter_2_out_5));
  substracter substracter_3 (
    .in_1(in_1[2]), .in_2(in_2[2]), .in_3(substracter_2_out_5), .out_4(out_3[2]), .out_5(substracter_3_out_5));
  substracter substracter_4 (
    .in_1(in_1[3]), .in_2(in_2[3]), .in_3(substracter_3_out_5), .out_4(out_3[3]), .out_5(substracter_4_out_5));
  substracter substracter_5 (
    .in_1(in_1[4]), .in_2(in_2[4]), .in_3(substracter_4_out_5), .out_4(out_3[4]), .out_5(substracter_5_out_5));
  substracter substracter_6 (
    .in_1(in_1[5]), .in_2(in_2[5]), .in_3(substracter_5_out_5), .out_4(out_3[5]), .out_5(substracter_6_out_5));
  substracter substracter_7 (
    .in_1(in_1[6]), .in_2(in_2[6]), .in_3(substracter_6_out_5), .out_4(out_3[6]), .out_5(substracter_7_out_5));
  substracter substracter_8 (
    .in_1(in_1[7]), .in_2(in_2[7]), .in_3(substracter_7_out_5), .out_4(out_3[7]), .out_5(out_4));
endmodule

module half_adder (
  input  in_1,
  input  in_2,
  output out_3,
  output out_4
);

  xor xor_1 (out_3, in_1, in_2);
  and and_1 (out_4, in_1, in_2);
endmodule

module adder (
  input  in_1,
  input  in_2,
  input  in_3,
  output out_4,
  output out_5
);

  wire half_adder_1_out_4, undriven, undriven_2;

  half_adder half_adder_1 (.in_1(in_1), .in_2(undriven_2), .out_3(out_4), .out_4(half_adder_1_out_4));
  or or_1 (out_5, half_adder_1_out_4, undriven);
endmodule

module deMUX (
  input  in_1,
  input  [1:0] in_2,
  output out_3,
  output out_4,
  output out_5,
  output out_6
);

  wire and_1_out, not_1_out, not_2_out;

  not not_1 (not_1_out, in_2[0]);
  not not_2 (not_2_out, in_2[1]);
  and and_1 (and_1_out, not_1_out, not_2_out);
  and and_2 (out_3, in_1, and_1_out);
  buf and_3 (out_4, in_1);  // AND_Gate
  buf and_4 (out_5, in_1);  // AND_Gate
  buf and_5 (out_6, in_1);  // AND_Gate
endmodule
