// Logisim project baranov1.circ as structural Verilog: 66 circuits, main circuit byte AND
module byte_AND (
  input  [7:0] in_1,
  input  [7:0] in_2,
  output [7:0] out_3
);

  assign out_3 = in_1 & in_2;  // AND_Gate and_1, 8 bits wide
endmodule

module byte_OR (
  input  [7:0] in_1,
  input  [7:0] in_2,
  output [7:0] out_3
);

  assign out_3 = in_1 | in_1 | in_2;  // OR_Gate or_1, 8 bits wide

  // Notes on the sheet:
  //   TIMOFEENKO
endmodule

module byte_XOR (
  input  [7:0] in_1,
  input  [7:0] in_2,
  output [7:0] out_3
);

  assign out_3 = in_1 ^ in_2;  // XOR_Gate xor_1, 8 bits wide

  // Notes on the sheet:
  //   TIMOFEENKO
endmodule

module byte_NOT (
  input  [7:0] in_1,
  output [7:0] out_2
);

  assign out_2 = ~in_1;  // NOT_Gate not_1, 8 bits wide

  // Notes on the sheet:
  //   TIMOFEENKO
endmodule

module logical_AND (
  input  [7:0] in_1,
  input  [7:0] in_2,
  output out_3
);

  wire or_1_out, or_2_out;

  or or_1 (or_1_out, in_1[0], in_1[1], in_1[2], in_1[3], in_1[4], in_1[5], in_1[6], in_1[7]);
  or or_2 (or_2_out, in_2[0], in_2[1], in_2[2], in_2[3], in_2[4], in_2[5], in_2[6], in_2[7]);
  and and_1 (out_3, or_1_out, or_2_out);

  // Notes on the sheet:
  //   TIMOFEENKO
endmodule

module logical_OR (
  input  [7:0] in_1,
  input  [7:0] in_2,
  output out_3
);

  wire or_1_out, or_2_out;

  or or_1 (or_1_out, in_1[0], in_1[1], in_1[2], in_1[3], in_1[4], in_1[5], in_1[6], in_1[7]);
  or or_2 (or_2_out, in_2[0], in_2[1], in_2[2], in_2[3], in_2[4], in_2[5], in_2[6], in_2[7]);
  or or_3 (out_3, or_1_out, or_2_out);

  // Notes on the sheet:
  //   TIMOFEENKO
endmodule

module logical_XOR (
  input  [7:0] in_1,
  input  [7:0] in_2,
  output out_3
);

  wire or_1_out, or_2_out;

  or or_1 (or_1_out, in_1[0], in_1[1], in_1[2], in_1[3], in_1[4], in_1[5], in_1[6], in_1[7]);
  or or_2 (or_2_out, in_2[0], in_2[1], in_2[2], in_2[3], in_2[4], in_2[5], in_2[6], in_2[7]);
  xor xor_1 (out_3, or_1_out, or_2_out);

  // Notes on the sheet:
  //   TIMOFEENKO
endmodule

module logical_NOT (
  input  [7:0] in_1,
  output out_2
);

  wire [7:0] byte_not_1_out_2;

  byte_NOT byte_not_1 (.in_1(in_1), .out_2(byte_not_1_out_2));
  or or_1 (out_2, byte_not_1_out_2[0], byte_not_1_out_2[1], byte_not_1_out_2[2], byte_not_1_out_2[3], byte_not_1_out_2[4], byte_not_1_out_2[5], byte_not_1_out_2[6], byte_not_1_out_2[7]);

  // Notes on the sheet:
  //   TIMOFEENKO
endmodule

module logical_shr_1_bit (
  input  [7:0] in_1,
  output [7:0] out_2
);


  assign out_2 = {1'b0, in_1[7:1]};
endmodule

module logical_shl_1_bit (
  input  [7:0] in_1,
  output [7:0] out_2
);


  assign out_2 = {in_1[6:0], 1'b0};
endmodule

module arifmetical_shr_1_bit (
  input  [7:0] in_1,
  output [7:0] out_2
);


  assign out_2 = {{2{in_1[7]}}, in_1[6:1]};
endmodule

module arifmetical_shl_1_bit (
  input  [7:0] in_1,
  output [7:0] out_2
);


  assign out_2 = {in_1[6:0], in_1[0]};
endmodule

module circular_shr_1_bit (
  input  [7:0] in_1,
  output [7:0] out_2
);


  assign out_2 = {in_1[0], in_1[7:1]};
endmodule

module curcular_shl_1_bit (
  input  [7:0] in_1,
  output [7:0] out_2
);


  assign out_2 = {in_1[6:0], in_1[7]};
endmodule

module cmp1 (
  input  in_1,
  input  in_2,
  output out_3,
  output out_4,
  output out_5
);

  wire not_1_out, not_2_out, xor_1_out;

  not not_1 (not_1_out, in_1);
  not not_2 (not_2_out, in_2);
  and and_1 (out_3, not_1_out, in_2);
  xor xor_1 (xor_1_out, in_1, in_2);
  and and_2 (out_5, in_1, not_2_out);
  not not_3 (out_4, xor_1_out);
endmodule

module cmp2 (
  input  _0,
  input  _1,
  input  _0_2,
  input  _1_2,
  output out_5,
  output out_6,
  output out_7
);

  wire and_1_out, and_2_out, cmp1_1_out_3, cmp1_1_out_4, cmp1_1_out_5, cmp1_2_out_3, cmp1_2_out_4,
       cmp1_2_out_5;

  cmp1 cmp1_1 (.in_1(_0), .in_2(_0_2), .out_3(cmp1_1_out_3), .out_4(cmp1_1_out_4), .out_5(cmp1_1_out_5));
  cmp1 cmp1_2 (.in_1(_1), .in_2(_1_2), .out_3(cmp1_2_out_3), .out_4(cmp1_2_out_4), .out_5(cmp1_2_out_5));
  and and_1 (and_1_out, cmp1_1_out_5, cmp1_2_out_4);
  and and_2 (and_2_out, cmp1_1_out_3, cmp1_2_out_4);
  and and_3 (out_5, cmp1_1_out_4, cmp1_2_out_4);
  or or_1 (out_6, and_1_out, cmp1_2_out_5);
  or or_2 (out_7, and_2_out, cmp1_2_out_3);

  // Notes on the sheet:
  //   B
  //   A
endmodule

module MUX (
  input  in_1,
  input  in_2,
  input  in_3,
  input  in_4,
  input  [1:0] in_5,
  output out_6
);

  wire and_1_out, and_2_out, and_3_out, and_4_out, not_1_out, not_2_out, not_3_out, not_4_out;

  not not_1 (not_1_out, in_5[1]);
  not not_2 (not_2_out, in_5[0]);
  not not_3 (not_3_out, in_5[1]);
  not not_4 (not_4_out, in_5[0]);
  and and_1 (and_1_out, in_1, not_1_out, not_2_out);
  and and_2 (and_2_out, in_2, in_5[0], not_3_out);
  and and_3 (and_3_out, in_3, in_5[1], not_4_out);
  and and_4 (and_4_out, in_4, in_5[0], in_5[1]);
  or or_1 (out_6, and_1_out, and_2_out, and_3_out, and_4_out);
endmodule

module logic_shr (
  input  [2:0] in_1,
  input  [7:0] in_2,
  output [7:0] out_3
);

  wire multiplexer_1_out, multiplexer_2_out, multiplexer_3_out, multiplexer_4_out, multiplexer_5_out,
       multiplexer_6_out, multiplexer_7_out, multiplexer_8_out, multiplexer_9_out, multiplexer_10_out,
       multiplexer_11_out, multiplexer_12_out, multiplexer_13_out, multiplexer_14_out, multiplexer_15_out,
       multiplexer_16_out, not_1_out, not_2_out, not_3_out;

  not not_1 (not_1_out, in_1[2]);
  not not_2 (not_2_out, in_1[1]);
  not not_3 (not_3_out, in_1[0]);
  Multiplexer multiplexer_1 (.in0(1'b0), .in1(in_2[7]), .out(multiplexer_1_out), .sel(not_3_out));  // open: en
  Multiplexer multiplexer_2 (.in0(in_2[7]), .in1(in_2[6]), .out(multiplexer_2_out), .sel(not_3_out));  // open: en
  Multiplexer multiplexer_3 (.in0(in_2[6]), .in1(in_2[5]), .out(multiplexer_3_out), .sel(not_3_out));  // open: en
  Multiplexer multiplexer_4 (.in0(in_2[5]), .in1(in_2[4]), .out(multiplexer_4_out), .sel(not_3_out));  // open: en
  Multiplexer multiplexer_5 (.in0(in_2[4]), .in1(in_2[3]), .out(multiplexer_5_out), .sel(not_3_out));  // open: en
  Multiplexer multiplexer_6 (.in0(in_2[3]), .in1(in_2[2]), .out(multiplexer_6_out), .sel(not_3_out));  // open: en
  Multiplexer multiplexer_7 (.in0(in_2[2]), .in1(in_2[1]), .out(multiplexer_7_out), .sel(not_3_out));  // open: en
  Multiplexer multiplexer_8 (.in0(in_2[1]), .in1(in_2[0]), .out(multiplexer_8_out), .sel(not_3_out));  // open: en
  Multiplexer multiplexer_9 (
    .in0(1'b0), .in1(multiplexer_1_out), .out(multiplexer_9_out), .sel(not_2_out));  // open: en
  Multiplexer multiplexer_10 (
    .in0(1'b0), .in1(multiplexer_2_out), .out(multiplexer_10_out), .sel(not_2_out));  // open: en
  Multiplexer multiplexer_11 (
    .in0(multiplexer_1_out), .in1(multiplexer_3_out), .out(multiplexer_11_out), .sel(not_2_out));  // open: en
  Multiplexer multiplexer_12 (
    .in0(multiplexer_2_out), .in1(multiplexer_4_out), .out(multiplexer_12_out), .sel(not_2_out));  // open: en
  Multiplexer multiplexer_13 (
    .in0(multiplexer_3_out), .in1(multiplexer_5_out), .out(multiplexer_13_out), .sel(not_2_out));  // open: en
  Multiplexer multiplexer_14 (
    .in0(multiplexer_4_out), .in1(multiplexer_6_out), .out(multiplexer_14_out), .sel(not_2_out));  // open: en
  Multiplexer multiplexer_15 (
    .in0(multiplexer_5_out), .in1(multiplexer_7_out), .out(multiplexer_15_out), .sel(not_2_out));  // open: en
  Multiplexer multiplexer_16 (
    .in0(multiplexer_6_out), .in1(multiplexer_8_out), .out(multiplexer_16_out), .sel(not_2_out));  // open: en
  Multiplexer multiplexer_17 (.in0(1'b0), .in1(multiplexer_9_out), .out(out_3[7]), .sel(not_1_out));  // open: en
  Multiplexer multiplexer_18 (.in0(1'b0), .in1(multiplexer_10_out), .out(out_3[6]), .sel(not_1_out));  // open: en
  Multiplexer multiplexer_19 (.in0(1'b0), .in1(multiplexer_11_out), .out(out_3[5]), .sel(not_1_out));  // open: en
  Multiplexer multiplexer_20 (.in0(1'b0), .in1(multiplexer_12_out), .out(out_3[4]), .sel(not_1_out));  // open: en
  Multiplexer multiplexer_21 (
    .in0(multiplexer_9_out), .in1(multiplexer_13_out), .out(out_3[3]), .sel(not_1_out));  // open: en
  Multiplexer multiplexer_22 (
    .in0(multiplexer_10_out), .in1(multiplexer_14_out), .out(out_3[2]), .sel(not_1_out));  // open: en
  Multiplexer multiplexer_23 (
    .in0(multiplexer_11_out), .in1(multiplexer_15_out), .out(out_3[1]), .sel(not_1_out));  // open: en
  Multiplexer multiplexer_24 (
    .in0(multiplexer_12_out), .in1(multiplexer_16_out), .out(out_3[0]), .sel(not_1_out));  // open: en
endmodule

module \unsigned  (
  input  [7:0] in_1,
  input  [7:0] in_2,
  output out_3
);

  wire less_8_bit_no_sign_1_out_3;

  less_8_bit_no_sign less_8_bit_no_sign_1 (.in_1(in_1), .in_2(in_2), .out_3(less_8_bit_no_sign_1_out_3));
  not not_1 (out_3, less_8_bit_no_sign_1_out_3);
endmodule

module logic_shl (
  input  [2:0] in_1,
  input  [7:0] in_2,
  output [7:0] out_3
);

  wire multiplexer_1_out, multiplexer_2_out, multiplexer_3_out, multiplexer_4_out, multiplexer_5_out,
       multiplexer_6_out, multiplexer_7_out, multiplexer_8_out, multiplexer_9_out, multiplexer_10_out,
       multiplexer_11_out, multiplexer_12_out, multiplexer_13_out, multiplexer_14_out, multiplexer_15_out,
       multiplexer_16_out, not_1_out, not_2_out, not_3_out;

  not not_1 (not_1_out, in_1[2]);
  not not_2 (not_2_out, in_1[1]);
  not not_3 (not_3_out, in_1[0]);
  Multiplexer multiplexer_1 (.in0(1'b0), .in1(in_2[0]), .out(multiplexer_1_out), .sel(not_3_out));  // open: en
  Multiplexer multiplexer_2 (.in0(in_2[0]), .in1(in_2[1]), .out(multiplexer_2_out), .sel(not_3_out));  // open: en
  Multiplexer multiplexer_3 (.in0(in_2[1]), .in1(in_2[2]), .out(multiplexer_3_out), .sel(not_3_out));  // open: en
  Multiplexer multiplexer_4 (.in0(in_2[2]), .in1(in_2[3]), .out(multiplexer_4_out), .sel(not_3_out));  // open: en
  Multiplexer multiplexer_5 (.in0(in_2[3]), .in1(in_2[4]), .out(multiplexer_5_out), .sel(not_3_out));  // open: en
  Multiplexer multiplexer_6 (.in0(in_2[4]), .in1(in_2[5]), .out(multiplexer_6_out), .sel(not_3_out));  // open: en
  Multiplexer multiplexer_7 (.in0(in_2[5]), .in1(in_2[6]), .out(multiplexer_7_out), .sel(not_3_out));  // open: en
  Multiplexer multiplexer_8 (.in0(in_2[6]), .in1(in_2[7]), .out(multiplexer_8_out), .sel(not_3_out));  // open: en
  Multiplexer multiplexer_9 (
    .in0(1'b0), .in1(multiplexer_1_out), .out(multiplexer_9_out), .sel(not_2_out));  // open: en
  Multiplexer multiplexer_10 (
    .in0(1'b0), .in1(multiplexer_2_out), .out(multiplexer_10_out), .sel(not_2_out));  // open: en
  Multiplexer multiplexer_11 (
    .in0(multiplexer_1_out), .in1(multiplexer_3_out), .out(multiplexer_11_out), .sel(not_2_out));  // open: en
  Multiplexer multiplexer_12 (
    .in0(multiplexer_2_out), .in1(multiplexer_4_out), .out(multiplexer_12_out), .sel(not_2_out));  // open: en
  Multiplexer multiplexer_13 (
    .in0(multiplexer_3_out), .in1(multiplexer_5_out), .out(multiplexer_13_out), .sel(not_2_out));  // open: en
  Multiplexer multiplexer_14 (
    .in0(multiplexer_4_out), .in1(multiplexer_6_out), .out(multiplexer_14_out), .sel(not_2_out));  // open: en
  Multiplexer multiplexer_15 (
    .in0(multiplexer_5_out), .in1(multiplexer_7_out), .out(multiplexer_15_out), .sel(not_2_out));  // open: en
  Multiplexer multiplexer_16 (
    .in0(multiplexer_6_out), .in1(multiplexer_8_out), .out(multiplexer_16_out), .sel(not_2_out));  // open: en
  Multiplexer multiplexer_17 (.in0(1'b0), .in1(multiplexer_9_out), .out(out_3[0]), .sel(not_1_out));  // open: en
  Multiplexer multiplexer_18 (.in0(1'b0), .in1(multiplexer_10_out), .out(out_3[1]), .sel(not_1_out));  // open: en
  Multiplexer multiplexer_19 (.in0(1'b0), .in1(multiplexer_11_out), .out(out_3[2]), .sel(not_1_out));  // open: en
  Multiplexer multiplexer_20 (.in0(1'b0), .in1(multiplexer_12_out), .out(out_3[3]), .sel(not_1_out));  // open: en
  Multiplexer multiplexer_21 (
    .in0(multiplexer_9_out), .in1(multiplexer_13_out), .out(out_3[4]), .sel(not_1_out));  // open: en
  Multiplexer multiplexer_22 (
    .in0(multiplexer_10_out), .in1(multiplexer_14_out), .out(out_3[5]), .sel(not_1_out));  // open: en
  Multiplexer multiplexer_23 (
    .in0(multiplexer_11_out), .in1(multiplexer_15_out), .out(out_3[6]), .sel(not_1_out));  // open: en
  Multiplexer multiplexer_24 (
    .in0(multiplexer_12_out), .in1(multiplexer_16_out), .out(out_3[7]), .sel(not_1_out));  // open: en
endmodule

module arifmetical_shr (
  input  [2:0] in_1,
  input  [7:0] in_2,
  output [7:0] out_3
);

  wire multiplexer_1_out, multiplexer_2_out, multiplexer_3_out, multiplexer_4_out, multiplexer_5_out,
       multiplexer_6_out, multiplexer_7_out, multiplexer_8_out, multiplexer_9_out, multiplexer_10_out,
       multiplexer_11_out, multiplexer_12_out, multiplexer_13_out, multiplexer_14_out, multiplexer_15_out,
       multiplexer_16_out, not_1_out, not_2_out, not_3_out;

  not not_1 (not_1_out, in_1[2]);
  not not_2 (not_2_out, in_1[1]);
  not not_3 (not_3_out, in_1[0]);
  Multiplexer multiplexer_1 (.in0(in_2[7]), .in1(in_2[7]), .out(multiplexer_1_out), .sel(not_3_out));  // open: en
  Multiplexer multiplexer_2 (.in0(in_2[7]), .in1(in_2[6]), .out(multiplexer_2_out), .sel(not_3_out));  // open: en
  Multiplexer multiplexer_3 (.in0(in_2[6]), .in1(in_2[5]), .out(multiplexer_3_out), .sel(not_3_out));  // open: en
  Multiplexer multiplexer_4 (.in0(in_2[5]), .in1(in_2[4]), .out(multiplexer_4_out), .sel(not_3_out));  // open: en
  Multiplexer multiplexer_5 (.in0(in_2[4]), .in1(in_2[3]), .out(multiplexer_5_out), .sel(not_3_out));  // open: en
  Multiplexer multiplexer_6 (.in0(in_2[3]), .in1(in_2[2]), .out(multiplexer_6_out), .sel(not_3_out));  // open: en
  Multiplexer multiplexer_7 (.in0(in_2[2]), .in1(in_2[1]), .out(multiplexer_7_out), .sel(not_3_out));  // open: en
  Multiplexer multiplexer_8 (.in0(in_2[1]), .in1(in_2[0]), .out(multiplexer_8_out), .sel(not_3_out));  // open: en
  Multiplexer multiplexer_9 (
    .in0(in_2[7]), .in1(multiplexer_1_out), .out(multiplexer_9_out), .sel(not_2_out));  // open: en
  Multiplexer multiplexer_10 (
    .in0(in_2[7]), .in1(multiplexer_2_out), .out(multiplexer_10_out), .sel(not_2_out));  // open: en
  Multiplexer multiplexer_11 (
    .in0(multiplexer_1_out), .in1(multiplexer_3_out), .out(multiplexer_11_out), .sel(not_2_out));  // open: en
  Multiplexer multiplexer_12 (
    .in0(multiplexer_2_out), .in1(multiplexer_4_out), .out(multiplexer_12_out), .sel(not_2_out));  // open: en
  Multiplexer multiplexer_13 (
    .in0(multiplexer_3_out), .in1(multiplexer_5_out), .out(multiplexer_13_out), .sel(not_2_out));  // open: en
  Multiplexer multiplexer_14 (
    .in0(multiplexer_4_out), .in1(multiplexer_6_out), .out(multiplexer_14_out), .sel(not_2_out));  // open: en
  Multiplexer multiplexer_15 (
    .in0(multiplexer_5_out), .in1(multiplexer_7_out), .out(multiplexer_15_out), .sel(not_2_out));  // open: en
  Multiplexer multiplexer_16 (
    .in0(multiplexer_6_out), .in1(multiplexer_8_out), .out(multiplexer_16_out), .sel(not_2_out));  // open: en
  Multiplexer multiplexer_17 (.in0(in_2[7]), .in1(multiplexer_9_out), .out(out_3[7]), .sel(not_1_out));  // open: en
  Multiplexer multiplexer_18 (.in0(in_2[7]), .in1(multiplexer_10_out), .out(out_3[6]), .sel(not_1_out));  // open: en
  Multiplexer multiplexer_19 (.in0(in_2[7]), .in1(multiplexer_11_out), .out(out_3[5]), .sel(not_1_out));  // open: en
  Multiplexer multiplexer_20 (.in0(in_2[7]), .in1(multiplexer_12_out), .out(out_3[4]), .sel(not_1_out));  // open: en
  Multiplexer multiplexer_21 (
    .in0(multiplexer_9_out), .in1(multiplexer_13_out), .out(out_3[3]), .sel(not_1_out));  // open: en
  Multiplexer multiplexer_22 (
    .in0(multiplexer_10_out), .in1(multiplexer_14_out), .out(out_3[2]), .sel(not_1_out));  // open: en
  Multiplexer multiplexer_23 (
    .in0(multiplexer_11_out), .in1(multiplexer_15_out), .out(out_3[1]), .sel(not_1_out));  // open: en
  Multiplexer multiplexer_24 (
    .in0(multiplexer_12_out), .in1(multiplexer_16_out), .out(out_3[0]), .sel(not_1_out));  // open: en
endmodule

module arifmetical_shl (
  input  [2:0] in_1,
  input  [7:0] in_2,
  output [7:0] out_3,
  output out_4
);

  wire and_1_out, and_2_out, and_3_out, multiplexer_1_out, multiplexer_2_out, multiplexer_3_out,
       multiplexer_4_out, multiplexer_5_out, multiplexer_6_out, multiplexer_7_out, multiplexer_8_out,
       multiplexer_9_out, multiplexer_10_out, multiplexer_11_out, multiplexer_12_out, multiplexer_13_out,
       multiplexer_14_out, multiplexer_15_out, multiplexer_16_out, not_1_out, not_2_out, not_3_out,
       not_4_out, not_5_out, not_6_out, or_1_out, or_2_out, or_3_out;

  not not_1 (not_1_out, in_1[2]);
  not not_2 (not_2_out, in_1[1]);
  not not_3 (not_3_out, in_1[0]);
  Multiplexer multiplexer_1 (.in0(in_2[0]), .in1(in_2[0]), .out(multiplexer_1_out), .sel(not_3_out));  // open: en
  Multiplexer multiplexer_2 (.in0(in_2[0]), .in1(in_2[1]), .out(multiplexer_2_out), .sel(not_3_out));  // open: en
  Multiplexer multiplexer_3 (.in0(in_2[1]), .in1(in_2[2]), .out(multiplexer_3_out), .sel(not_3_out));  // open: en
  Multiplexer multiplexer_4 (.in0(in_2[2]), .in1(in_2[3]), .out(multiplexer_4_out), .sel(not_3_out));  // open: en
  Multiplexer multiplexer_5 (.in0(in_2[3]), .in1(in_2[4]), .out(multiplexer_5_out), .sel(not_3_out));  // open: en
  Multiplexer multiplexer_6 (.in0(in_2[4]), .in1(in_2[5]), .out(multiplexer_6_out), .sel(not_3_out));  // open: en
  Multiplexer multiplexer_7 (.in0(in_2[5]), .in1(in_2[6]), .out(multiplexer_7_out), .sel(not_3_out));  // open: en
  Multiplexer multiplexer_8 (.in0(in_2[6]), .in1(in_2[7]), .out(multiplexer_8_out), .sel(not_3_out));  // open: en
  not not_4 (not_4_out, not_3_out);
  and and_1 (and_1_out, not_4_out, in_2[7]);
  Multiplexer multiplexer_9 (
    .in0(in_2[0]), .in1(multiplexer_1_out), .out(multiplexer_9_out), .sel(not_2_out));  // open: en
  Multiplexer multiplexer_10 (
    .in0(in_2[0]), .in1(multiplexer_2_out), .out(multiplexer_10_out), .sel(not_2_out));  // open: en
  Multiplexer multiplexer_11 (
    .in0(multiplexer_1_out), .in1(multiplexer_3_out), .out(multiplexer_11_out), .sel(not_2_out));  // open: en
  Multiplexer multiplexer_12 (
    .in0(multiplexer_2_out), .in1(multiplexer_4_out), .out(multiplexer_12_out), .sel(not_2_out));  // open: en
  Multiplexer multiplexer_13 (
    .in0(multiplexer_3_out), .in1(multiplexer_5_out), .out(multiplexer_13_out), .sel(not_2_out));  // open: en
  Multiplexer multiplexer_14 (
    .in0(multiplexer_4_out), .in1(multiplexer_6_out), .out(multiplexer_14_out), .sel(not_2_out));  // open: en
  Multiplexer multiplexer_15 (
    .in0(multiplexer_5_out), .in1(multiplexer_7_out), .out(multiplexer_15_out), .sel(not_2_out));  // open: en
  Multiplexer multiplexer_16 (
    .in0(multiplexer_6_out), .in1(multiplexer_8_out), .out(multiplexer_16_out), .sel(not_2_out));  // open: en
  not not_5 (not_5_out, not_2_out);
  or or_1 (or_1_out, multiplexer_7_out, multiplexer_8_out);
  or or_2 (or_2_out, and_2_out, and_1_out);
  and and_2 (and_2_out, not_5_out, or_1_out);
  Multiplexer multiplexer_17 (.in0(in_2[0]), .in1(multiplexer_9_out), .out(out_3[0]), .sel(not_1_out));  // open: en
  Multiplexer multiplexer_18 (.in0(in_2[0]), .in1(multiplexer_10_out), .out(out_3[1]), .sel(not_1_out));  // open: en
  Multiplexer multiplexer_19 (.in0(in_2[0]), .in1(multiplexer_11_out), .out(out_3[2]), .sel(not_1_out));  // open: en
  Multiplexer multiplexer_20 (.in0(in_2[0]), .in1(multiplexer_12_out), .out(out_3[3]), .sel(not_1_out));  // open: en
  Multiplexer multiplexer_21 (
    .in0(multiplexer_9_out), .in1(multiplexer_13_out), .out(out_3[4]), .sel(not_1_out));  // open: en
  Multiplexer multiplexer_22 (
    .in0(multiplexer_10_out), .in1(multiplexer_14_out), .out(out_3[5]), .sel(not_1_out));  // open: en
  Multiplexer multiplexer_23 (
    .in0(multiplexer_11_out), .in1(multiplexer_15_out), .out(out_3[6]), .sel(not_1_out));  // open: en
  Multiplexer multiplexer_24 (
    .in0(multiplexer_12_out), .in1(multiplexer_16_out), .out(out_3[7]), .sel(not_1_out));  // open: en
  or or_3 (or_3_out, multiplexer_16_out, multiplexer_15_out, multiplexer_14_out, multiplexer_13_out);
  not not_6 (not_6_out, not_1_out);
  and and_3 (and_3_out, not_6_out, or_3_out);
  or or_4 (out_4, and_3_out, or_2_out);
endmodule

module cycle_shr (
  input  [2:0] in_1,
  input  [7:0] in_2,
  output [7:0] out_3
);

  wire multiplexer_1_out, multiplexer_2_out, multiplexer_3_out, multiplexer_4_out, multiplexer_5_out,
       multiplexer_6_out, multiplexer_7_out, multiplexer_8_out, multiplexer_9_out, multiplexer_10_out,
       multiplexer_11_out, multiplexer_12_out, multiplexer_13_out, multiplexer_14_out, multiplexer_15_out,
       multiplexer_16_out;

  Multiplexer multiplexer_1 (.in0(in_2[7]), .in1(in_2[0]), .out(multiplexer_1_out), .sel(in_1[0]));  // open: en
  Multiplexer multiplexer_2 (.in0(in_2[0]), .in1(in_2[1]), .out(multiplexer_2_out), .sel(in_1[0]));  // open: en
  Multiplexer multiplexer_3 (.in0(in_2[1]), .in1(in_2[2]), .out(multiplexer_3_out), .sel(in_1[0]));  // open: en
  Multiplexer multiplexer_4 (.in0(in_2[2]), .in1(in_2[3]), .out(multiplexer_4_out), .sel(in_1[0]));  // open: en
  Multiplexer multiplexer_5 (.in0(in_2[3]), .in1(in_2[4]), .out(multiplexer_5_out), .sel(in_1[0]));  // open: en
  Multiplexer multiplexer_6 (.in0(in_2[4]), .in1(in_2[5]), .out(multiplexer_6_out), .sel(in_1[0]));  // open: en
  Multiplexer multiplexer_7 (.in0(in_2[5]), .in1(in_2[6]), .out(multiplexer_7_out), .sel(in_1[0]));  // open: en
  Multiplexer multiplexer_8 (.in0(in_2[6]), .in1(in_2[7]), .out(multiplexer_8_out), .sel(in_1[0]));  // open: en
  Multiplexer multiplexer_9 (
    .in0(multiplexer_7_out), .in1(multiplexer_1_out), .out(multiplexer_9_out), .sel(in_1[1]));  // open: en
  Multiplexer multiplexer_10 (
    .in0(multiplexer_8_out), .in1(multiplexer_2_out), .out(multiplexer_10_out), .sel(in_1[1]));  // open: en
  Multiplexer multiplexer_11 (
    .in0(multiplexer_1_out), .in1(multiplexer_3_out), .out(multiplexer_11_out), .sel(in_1[1]));  // open: en
  Multiplexer multiplexer_12 (
    .in0(multiplexer_2_out), .in1(multiplexer_4_out), .out(multiplexer_12_out), .sel(in_1[1]));  // open: en
  Multiplexer multiplexer_13 (
    .in0(multiplexer_3_out), .in1(multiplexer_5_out), .out(multiplexer_13_out), .sel(in_1[1]));  // open: en
  Multiplexer multiplexer_14 (
    .in0(multiplexer_4_out), .in1(multiplexer_6_out), .out(multiplexer_14_out), .sel(in_1[1]));  // open: en
  Multiplexer multiplexer_15 (
    .in0(multiplexer_5_out), .in1(multiplexer_7_out), .out(multiplexer_15_out), .sel(in_1[1]));  // open: en
  Multiplexer multiplexer_16 (
    .in0(multiplexer_6_out), .in1(multiplexer_8_out), .out(multiplexer_16_out), .sel(in_1[1]));  // open: en
  Multiplexer multiplexer_17 (
    .in0(multiplexer_13_out), .in1(multiplexer_9_out), .out(out_3[0]), .sel(in_1[2]));  // open: en
  Multiplexer multiplexer_18 (
    .in0(multiplexer_14_out), .in1(multiplexer_10_out), .out(out_3[1]), .sel(in_1[2]));  // open: en
  Multiplexer multiplexer_19 (
    .in0(multiplexer_15_out), .in1(multiplexer_11_out), .out(out_3[2]), .sel(in_1[2]));  // open: en
  Multiplexer multiplexer_20 (
    .in0(multiplexer_16_out), .in1(multiplexer_12_out), .out(out_3[3]), .sel(in_1[2]));  // open: en
  Multiplexer multiplexer_21 (
    .in0(multiplexer_9_out), .in1(multiplexer_13_out), .out(out_3[4]), .sel(in_1[2]));  // open: en
  Multiplexer multiplexer_22 (
    .in0(multiplexer_10_out), .in1(multiplexer_14_out), .out(out_3[5]), .sel(in_1[2]));  // open: en
  Multiplexer multiplexer_23 (
    .in0(multiplexer_11_out), .in1(multiplexer_15_out), .out(out_3[6]), .sel(in_1[2]));  // open: en
  Multiplexer multiplexer_24 (
    .in0(multiplexer_12_out), .in1(multiplexer_16_out), .out(out_3[7]), .sel(in_1[2]));  // open: en
endmodule

module cycle_shl (
  input  [2:0] in_1,
  input  [7:0] in_2,
  output [7:0] out_3
);

  wire multiplexer_1_out, multiplexer_2_out, multiplexer_3_out, multiplexer_4_out, multiplexer_5_out,
       multiplexer_6_out, multiplexer_7_out, multiplexer_8_out, multiplexer_9_out, multiplexer_10_out,
       multiplexer_11_out, multiplexer_12_out, multiplexer_13_out, multiplexer_14_out, multiplexer_15_out,
       multiplexer_16_out;

  Multiplexer multiplexer_1 (.in0(in_2[0]), .in1(in_2[7]), .out(multiplexer_1_out), .sel(in_1[0]));  // open: en
  Multiplexer multiplexer_2 (.in0(in_2[7]), .in1(in_2[6]), .out(multiplexer_2_out), .sel(in_1[0]));  // open: en
  Multiplexer multiplexer_3 (.in0(in_2[6]), .in1(in_2[5]), .out(multiplexer_3_out), .sel(in_1[0]));  // open: en
  Multiplexer multiplexer_4 (.in0(in_2[5]), .in1(in_2[4]), .out(multiplexer_4_out), .sel(in_1[0]));  // open: en
  Multiplexer multiplexer_5 (.in0(in_2[4]), .in1(in_2[3]), .out(multiplexer_5_out), .sel(in_1[0]));  // open: en
  Multiplexer multiplexer_6 (.in0(in_2[3]), .in1(in_2[2]), .out(multiplexer_6_out), .sel(in_1[0]));  // open: en
  Multiplexer multiplexer_7 (.in0(in_2[2]), .in1(in_2[1]), .out(multiplexer_7_out), .sel(in_1[0]));  // open: en
  Multiplexer multiplexer_8 (.in0(in_2[1]), .in1(in_2[0]), .out(multiplexer_8_out), .sel(in_1[0]));  // open: en
  Multiplexer multiplexer_9 (
    .in0(multiplexer_7_out), .in1(multiplexer_1_out), .out(multiplexer_9_out), .sel(in_1[1]));  // open: en
  Multiplexer multiplexer_10 (
    .in0(multiplexer_8_out), .in1(multiplexer_2_out), .out(multiplexer_10_out), .sel(in_1[1]));  // open: en
  Multiplexer multiplexer_11 (
    .in0(multiplexer_1_out), .in1(multiplexer_3_out), .out(multiplexer_11_out), .sel(in_1[1]));  // open: en
  Multiplexer multiplexer_12 (
    .in0(multiplexer_2_out), .in1(multiplexer_4_out), .out(multiplexer_12_out), .sel(in_1[1]));  // open: en
  Multiplexer multiplexer_13 (
    .in0(multiplexer_3_out), .in1(multiplexer_5_out), .out(multiplexer_13_out), .sel(in_1[1]));  // open: en
  Multiplexer multiplexer_14 (
    .in0(multiplexer_4_out), .in1(multiplexer_6_out), .out(multiplexer_14_out), .sel(in_1[1]));  // open: en
  Multiplexer multiplexer_15 (
    .in0(multiplexer_5_out), .in1(multiplexer_7_out), .out(multiplexer_15_out), .sel(in_1[1]));  // open: en
  Multiplexer multiplexer_16 (
    .in0(multiplexer_6_out), .in1(multiplexer_8_out), .out(multiplexer_16_out), .sel(in_1[1]));  // open: en
  Multiplexer multiplexer_17 (
    .in0(multiplexer_13_out), .in1(multiplexer_9_out), .out(out_3[0]), .sel(in_1[2]));  // open: en
  Multiplexer multiplexer_18 (
    .in0(multiplexer_14_out), .in1(multiplexer_10_out), .out(out_3[7]), .sel(in_1[2]));  // open: en
  Multiplexer multiplexer_19 (
    .in0(multiplexer_15_out), .in1(multiplexer_11_out), .out(out_3[6]), .sel(in_1[2]));  // open: en
  Multiplexer multiplexer_20 (
    .in0(multiplexer_16_out), .in1(multiplexer_12_out), .out(out_3[5]), .sel(in_1[2]));  // open: en
  Multiplexer multiplexer_21 (
    .in0(multiplexer_9_out), .in1(multiplexer_13_out), .out(out_3[4]), .sel(in_1[2]));  // open: en
  Multiplexer multiplexer_22 (
    .in0(multiplexer_10_out), .in1(multiplexer_14_out), .out(out_3[3]), .sel(in_1[2]));  // open: en
  Multiplexer multiplexer_23 (
    .in0(multiplexer_11_out), .in1(multiplexer_15_out), .out(out_3[2]), .sel(in_1[2]));  // open: en
  Multiplexer multiplexer_24 (
    .in0(multiplexer_12_out), .in1(multiplexer_16_out), .out(out_3[1]), .sel(in_1[2]));  // open: en
endmodule

module less_1_bit (
  input  in_1,
  input  in_2,
  output out_3
);

  wire not_1_out;

  not not_1 (not_1_out, in_1);
  and and_1 (out_3, not_1_out, in_2);
endmodule

module not_more_1_bit (
  input  in_1,
  input  in_2,
  output out_3
);

  wire not_1_out;

  not not_1 (not_1_out, in_2);
  nand nand_1 (out_3, in_1, not_1_out);
endmodule

module less_8_bit_no_sign (
  input  [7:0] in_1,
  input  [7:0] in_2,
  output out_3
);

  wire and_1_out, and_2_out, and_3_out, and_4_out, and_5_out, and_6_out, and_7_out, less_1_bit_1_out_3,
       less_1_bit_2_out_3, less_1_bit_3_out_3, less_1_bit_4_out_3, less_1_bit_5_out_3, less_1_bit_6_out_3,
       less_1_bit_7_out_3, less_1_bit_8_out_3, not_more_1_bit_1_out_3, not_more_1_bit_2_out_3,
       not_more_1_bit_3_out_3, not_more_1_bit_4_out_3, not_more_1_bit_5_out_3, not_more_1_bit_6_out_3,
       not_more_1_bit_7_out_3;

  less_1_bit less_1_bit_1 (.in_1(in_1[7]), .in_2(in_2[7]), .out_3(less_1_bit_1_out_3));
  less_1_bit less_1_bit_2 (.in_1(in_1[6]), .in_2(in_2[6]), .out_3(less_1_bit_2_out_3));
  less_1_bit less_1_bit_3 (.in_1(in_1[5]), .in_2(in_2[5]), .out_3(less_1_bit_3_out_3));
  not_more_1_bit not_more_1_bit_1 (.in_1(in_1[7]), .in_2(in_2[7]), .out_3(not_more_1_bit_1_out_3));
  not_more_1_bit not_more_1_bit_2 (.in_1(in_1[6]), .in_2(in_2[6]), .out_3(not_more_1_bit_2_out_3));
  not_more_1_bit not_more_1_bit_3 (.in_1(in_1[5]), .in_2(in_2[5]), .out_3(not_more_1_bit_3_out_3));
  less_1_bit less_1_bit_4 (.in_1(in_1[4]), .in_2(in_2[4]), .out_3(less_1_bit_4_out_3));
  not_more_1_bit not_more_1_bit_4 (.in_1(in_1[4]), .in_2(in_2[4]), .out_3(not_more_1_bit_4_out_3));
  less_1_bit less_1_bit_5 (.in_1(in_1[3]), .in_2(in_2[3]), .out_3(less_1_bit_5_out_3));
  not_more_1_bit not_more_1_bit_5 (.in_1(in_1[3]), .in_2(in_2[3]), .out_3(not_more_1_bit_5_out_3));
  less_1_bit less_1_bit_6 (.in_1(in_1[2]), .in_2(in_2[2]), .out_3(less_1_bit_6_out_3));
  not_more_1_bit not_more_1_bit_6 (.in_1(in_1[2]), .in_2(in_2[2]), .out_3(not_more_1_bit_6_out_3));
  less_1_bit less_1_bit_7 (.in_1(in_1[1]), .in_2(in_2[1]), .out_3(less_1_bit_7_out_3));
  not_more_1_bit not_more_1_bit_7 (.in_1(in_1[1]), .in_2(in_2[1]), .out_3(not_more_1_bit_7_out_3));
  less_1_bit less_1_bit_8 (.in_1(in_1[0]), .in_2(in_2[0]), .out_3(less_1_bit_8_out_3));
  and and_1 (and_1_out, not_more_1_bit_1_out_3, less_1_bit_2_out_3);
  and and_2 (and_2_out, not_more_1_bit_1_out_3, not_more_1_bit_2_out_3, less_1_bit_3_out_3);
  and and_3 (and_3_out, not_more_1_bit_1_out_3, not_more_1_bit_2_out_3, not_more_1_bit_3_out_3, less_1_bit_4_out_3);
  and and_4 (and_4_out, not_more_1_bit_1_out_3, not_more_1_bit_2_out_3, not_more_1_bit_3_out_3, not_more_1_bit_4_out_3, less_1_bit_5_out_3);
  and and_5 (and_5_out, not_more_1_bit_1_out_3, not_more_1_bit_2_out_3, not_more_1_bit_3_out_3, not_more_1_bit_4_out_3, not_more_1_bit_5_out_3, less_1_bit_6_out_3);
  and and_6 (and_6_out, not_more_1_bit_1_out_3, not_more_1_bit_2_out_3, not_more_1_bit_3_out_3, not_more_1_bit_4_out_3, not_more_1_bit_5_out_3, not_more_1_bit_6_out_3, less_1_bit_7_out_3);
  and and_7 (and_7_out, not_more_1_bit_1_out_3, not_more_1_bit_2_out_3, not_more_1_bit_3_out_3, not_more_1_bit_4_out_3, not_more_1_bit_5_out_3, not_more_1_bit_6_out_3, not_more_1_bit_7_out_3, less_1_bit_8_out_3);
  or or_1 (out_3, less_1_bit_1_out_3, and_1_out, and_2_out, and_3_out, and_4_out, and_5_out, and_6_out, and_7_out);
endmodule

module bigger_8_bit_no_sign (
  input  [7:0] in_1,
  input  [7:0] in_2,
  output out_3
);

  less_8_bit_no_sign less_8_bit_no_sign_1 (.in_1(in_2), .in_2(in_1), .out_3(out_3));
endmodule

module equal_8_bit_no_sign (
  input  [7:0] in_1,
  input  [7:0] in_2,
  output out_3
);

  wire bigger_8_bit_no_sign_1_out_3, less_8_bit_no_sign_1_out_3, not_1_out, not_2_out;

  not not_1 (not_1_out, less_8_bit_no_sign_1_out_3);
  less_8_bit_no_sign less_8_bit_no_sign_1 (.in_1(in_1), .in_2(in_2), .out_3(less_8_bit_no_sign_1_out_3));
  bigger_8_bit_no_sign bigger_8_bit_no_sign_1 (.in_1(in_1), .in_2(in_2), .out_3(bigger_8_bit_no_sign_1_out_3));
  not not_2 (not_2_out, bigger_8_bit_no_sign_1_out_3);
  and and_1 (out_3, not_1_out, not_2_out);
endmodule

module less_or_equal_8_bit_no_sign (
  input  [7:0] in_1,
  input  [7:0] in_2,
  output out_3
);

  wire equal_8_bit_no_sign_1_out_3, less_8_bit_no_sign_1_out_3;

  less_8_bit_no_sign less_8_bit_no_sign_1 (.in_1(in_1), .in_2(in_2), .out_3(less_8_bit_no_sign_1_out_3));
  equal_8_bit_no_sign equal_8_bit_no_sign_1 (.in_1(in_1), .in_2(in_2), .out_3(equal_8_bit_no_sign_1_out_3));
  or or_1 (out_3, less_8_bit_no_sign_1_out_3, equal_8_bit_no_sign_1_out_3);
endmodule

module bigger_or_equal_8_bit_no_sign (
  input  [7:0] in_1,
  input  [7:0] in_2,
  output out_3
);

  wire bigger_8_bit_no_sign_1_out_3, equal_8_bit_no_sign_1_out_3;

  bigger_8_bit_no_sign bigger_8_bit_no_sign_1 (.in_1(in_1), .in_2(in_2), .out_3(bigger_8_bit_no_sign_1_out_3));
  equal_8_bit_no_sign equal_8_bit_no_sign_1 (.in_1(in_1), .in_2(in_2), .out_3(equal_8_bit_no_sign_1_out_3));
  or or_1 (out_3, bigger_8_bit_no_sign_1_out_3, equal_8_bit_no_sign_1_out_3);
endmodule

module not_equal_8_bit_no_sign (
  input  [7:0] in_1,
  input  [7:0] in_2,
  output out_3
);

  wire and_1_out, bigger_8_bit_no_sign_1_out_3, less_8_bit_no_sign_1_out_3, not_1_out, not_2_out;

  not not_1 (not_1_out, less_8_bit_no_sign_1_out_3);
  less_8_bit_no_sign less_8_bit_no_sign_1 (.in_1(in_1), .in_2(in_2), .out_3(less_8_bit_no_sign_1_out_3));
  not not_2 (not_2_out, bigger_8_bit_no_sign_1_out_3);
  bigger_8_bit_no_sign bigger_8_bit_no_sign_1 (.in_1(in_1), .in_2(in_2), .out_3(bigger_8_bit_no_sign_1_out_3));
  and and_1 (and_1_out, not_1_out, not_2_out);
  not not_3 (out_3, and_1_out);
endmodule

module less_7_bit_nosign (
  input  [6:0] in_1,
  input  [6:0] in_2,
  output out_3
);

  wire and_1_out, and_2_out, and_3_out, and_4_out, and_5_out, and_6_out, less_1_bit_1_out_3,
       less_1_bit_2_out_3, less_1_bit_3_out_3, less_1_bit_4_out_3, less_1_bit_5_out_3, less_1_bit_6_out_3,
       less_1_bit_7_out_3, not_more_1_bit_1_out_3, not_more_1_bit_2_out_3, not_more_1_bit_3_out_3,
       not_more_1_bit_4_out_3, not_more_1_bit_5_out_3, not_more_1_bit_6_out_3;

  less_1_bit less_1_bit_1 (.in_1(in_1[6]), .in_2(in_2[6]), .out_3(less_1_bit_1_out_3));
  less_1_bit less_1_bit_2 (.in_1(in_1[5]), .in_2(in_2[5]), .out_3(less_1_bit_2_out_3));
  less_1_bit less_1_bit_3 (.in_1(in_1[4]), .in_2(in_2[4]), .out_3(less_1_bit_3_out_3));
  not_more_1_bit not_more_1_bit_1 (.in_1(in_1[6]), .in_2(in_2[6]), .out_3(not_more_1_bit_1_out_3));
  not_more_1_bit not_more_1_bit_2 (.in_1(in_1[5]), .in_2(in_2[5]), .out_3(not_more_1_bit_2_out_3));
  not_more_1_bit not_more_1_bit_3 (.in_1(in_1[4]), .in_2(in_2[4]), .out_3(not_more_1_bit_3_out_3));
  less_1_bit less_1_bit_4 (.in_1(in_1[3]), .in_2(in_2[3]), .out_3(less_1_bit_4_out_3));
  not_more_1_bit not_more_1_bit_4 (.in_1(in_1[3]), .in_2(in_2[3]), .out_3(not_more_1_bit_4_out_3));
  less_1_bit less_1_bit_5 (.in_1(in_1[2]), .in_2(in_2[2]), .out_3(less_1_bit_5_out_3));
  not_more_1_bit not_more_1_bit_5 (.in_1(in_1[2]), .in_2(in_2[2]), .out_3(not_more_1_bit_5_out_3));
  less_1_bit less_1_bit_6 (.in_1(in_1[1]), .in_2(in_2[1]), .out_3(less_1_bit_6_out_3));
  not_more_1_bit not_more_1_bit_6 (.in_1(in_1[1]), .in_2(in_2[1]), .out_3(not_more_1_bit_6_out_3));
  less_1_bit less_1_bit_7 (.in_1(in_1[0]), .in_2(in_2[0]), .out_3(less_1_bit_7_out_3));
  and and_1 (and_1_out, not_more_1_bit_1_out_3, less_1_bit_2_out_3);
  and and_2 (and_2_out, not_more_1_bit_1_out_3, not_more_1_bit_2_out_3, less_1_bit_3_out_3);
  and and_3 (and_3_out, not_more_1_bit_1_out_3, not_more_1_bit_2_out_3, not_more_1_bit_3_out_3, less_1_bit_4_out_3);
  and and_4 (and_4_out, not_more_1_bit_1_out_3, not_more_1_bit_2_out_3, not_more_1_bit_3_out_3, not_more_1_bit_4_out_3, less_1_bit_5_out_3);
  and and_5 (and_5_out, not_more_1_bit_1_out_3, not_more_1_bit_2_out_3, not_more_1_bit_3_out_3, not_more_1_bit_4_out_3, not_more_1_bit_5_out_3, less_1_bit_6_out_3);
  and and_6 (and_6_out, not_more_1_bit_1_out_3, not_more_1_bit_2_out_3, not_more_1_bit_3_out_3, not_more_1_bit_4_out_3, not_more_1_bit_5_out_3, not_more_1_bit_6_out_3, less_1_bit_7_out_3);
  or or_1 (out_3, less_1_bit_1_out_3, and_1_out, and_2_out, and_3_out, and_4_out, and_5_out, and_6_out);
endmodule

module NOT (
  input  [7:0] in_1,
  output out_2
);

  wire [7:0] not_1_out;

  assign not_1_out = ~in_1;  // NOT_Gate not_1, 8 bits wide
  and and_1 (out_2, not_1_out[0], not_1_out[1], not_1_out[2], not_1_out[3], not_1_out[4], not_1_out[5], not_1_out[6], not_1_out[7]);
endmodule

module bigger_7_bit_no_sign (
  input  [6:0] in_1,
  input  [6:0] in_2,
  output out_3
);

  less_7_bit_nosign less_7_bit_nosign_1 (.in_1(in_2), .in_2(in_1), .out_3(out_3));
endmodule

module less_8__bit_sign (
  input  [7:0] in_1,
  input  [7:0] in_2,
  output out_3
);

  wire and_1_out, and_2_out, and_3_out, bigger_7_bit_no_sign_1_out_3, less_7_bit_nosign_1_out_3, not_1_out,
       not_2_out, not_3_out, not_4_out;

  not not_1 (not_1_out, in_2[7]);
  less_7_bit_nosign less_7_bit_nosign_1 (.in_1(in_1[6:0]), .in_2(in_2[6:0]), .out_3(less_7_bit_nosign_1_out_3));
  bigger_7_bit_no_sign bigger_7_bit_no_sign_1 (
    .in_1(in_1[6:0]), .in_2(in_2[6:0]), .out_3(bigger_7_bit_no_sign_1_out_3));
  not not_2 (not_2_out, bigger_7_bit_no_sign_1_out_3);
  and and_1 (and_1_out, in_1[7], not_3_out, bigger_7_bit_no_sign_1_out_3);
  not not_3 (not_3_out, less_7_bit_nosign_1_out_3);
  and and_2 (and_2_out, in_1[7], not_1_out, not_4_out);
  not not_4 (not_4_out, bigger_7_bit_no_sign_1_out_3);
  and and_3 (and_3_out, less_7_bit_nosign_1_out_3, not_2_out, not_1_out);
  or or_1 (out_3, and_1_out, and_2_out, and_3_out);
endmodule

module bigger_8_bit_sign (
  input  [7:0] in_1,
  input  [7:0] in_2,
  output out_3
);

  less_8__bit_sign less_8_bit_sign_1 (.in_1(in_2), .in_2(in_1), .out_3(out_3));
endmodule

module equal_8_bit_sign (
  input  [7:0] in_1,
  input  [7:0] in_2,
  output out_3
);

  wire bigger_8_bit_sign_1_out_3, less_8_bit_sign_1_out_3, not_1_out, not_2_out;

  less_8__bit_sign less_8_bit_sign_1 (.in_1(in_1), .in_2(in_2), .out_3(less_8_bit_sign_1_out_3));
  not not_1 (not_1_out, less_8_bit_sign_1_out_3);
  bigger_8_bit_sign bigger_8_bit_sign_1 (.in_1(in_1), .in_2(in_2), .out_3(bigger_8_bit_sign_1_out_3));
  not not_2 (not_2_out, bigger_8_bit_sign_1_out_3);
  and and_1 (out_3, not_1_out, not_2_out);
endmodule

module less_or_equal_8_bit_sign (
  input  [7:0] in_1,
  input  [7:0] in_2,
  output out_3
);

  wire equal_8_bit_sign_1_out_3, less_8_bit_sign_1_out_3;

  less_8__bit_sign less_8_bit_sign_1 (.in_1(in_1), .in_2(in_2), .out_3(less_8_bit_sign_1_out_3));
  equal_8_bit_sign equal_8_bit_sign_1 (.in_1(in_1), .in_2(in_2), .out_3(equal_8_bit_sign_1_out_3));
  or or_1 (out_3, less_8_bit_sign_1_out_3, equal_8_bit_sign_1_out_3);
endmodule

module bigger_or_equal_8_bit_sign (
  input  [7:0] in_1,
  input  [7:0] in_2,
  output out_3
);

  wire bigger_8_bit_sign_1_out_3, equal_8_bit_sign_1_out_3;

  bigger_8_bit_sign bigger_8_bit_sign_1 (.in_1(in_1), .in_2(in_2), .out_3(bigger_8_bit_sign_1_out_3));
  equal_8_bit_sign equal_8_bit_sign_1 (.in_1(in_1), .in_2(in_2), .out_3(equal_8_bit_sign_1_out_3));
  or or_1 (out_3, bigger_8_bit_sign_1_out_3, equal_8_bit_sign_1_out_3);
endmodule

module half_substracter (
  input  in_1,
  input  in_2,
  output out_3,
  output out_4
);

  wire not_1_out;

  not not_1 (not_1_out, in_1);
  xor xor_1 (out_3, in_1, in_2);
  and and_1 (out_4, not_1_out, in_2);
endmodule

module substracter (
  input  in_1,
  input  in_2,
  input  in_3,
  output out_4,
  output out_5
);

  wire half_substracter_1_out_3, half_substracter_1_out_4, half_substracter_2_out_4;

  half_substracter half_substracter_1 (
    .in_1(in_1), .in_2(in_2), .out_3(half_substracter_1_out_3), .out_4(half_substracter_1_out_4));
  half_substracter half_substracter_2 (
    .in_1(half_substracter_1_out_3), .in_2(in_3), .out_3(out_4), .out_4(half_substracter_2_out_4));
  or or_1 (out_5, half_substracter_2_out_4, half_substracter_1_out_4);
endmodule

module substracter_8_bit (
  input  [7:0] in_1,
  input  [7:0] in_2,
  output [7:0] out_3,
  output out_4
);

  wire substracter_1_out_5, substracter_2_out_5, substracter_3_out_5, substracter_4_out_5,
       substracter_5_out_5, substracter_6_out_5, substracter_7_out_5;

  substracter substracter_1 (
    .in_1(in_1[0]), .in_2(in_2[0]), .in_3(1'b0), .out_4(out_3[0]), .out_5(substracter_1_out_5));
  substracter substracter_2 (
    .in_1(in_1[1]), .in_2(in_2[1]), .in_3(substracter_1_out_5), .out_4(out_3[1]), .out_5(substracter_2_out_5));
  substracter substracter_3 (
    .in_1(in_1[2]), .in_2(in_2[2]), .in_3(substracter_2_out_5), .out_4(out_3[2]), .out_5(substracter_3_out_5));
  substracter substracter_4 (
    .in_1(in_1[3]), .in_2(in_2[3]), .in_3(substracter_3_out_5), .out_4(out_3[3]), .out_5(substracter_4_out_5));
  substracter substracter_5 (
    .in_1(in_1[4]), .in_2(in_2[4]), .in_3(substracter_4_out_5), .out_4(out_3[4]), .out_5(substracter_5_out_5));
  substracter substracter_6 (
    .in_1(in_1[5]), .in_2(in_2[5]), .in_3(substracter_5_out_5), .out_4(out_3[5]), .out_5(substracter_6_out_5));
  substracter substracter_7 (
    .in_1(in_1[6]), .in_2(in_2[6]), .in_3(substracter_6_out_5), .out_4(out_3[6]), .out_5(substracter_7_out_5));
  substracter substracter_8 (
    .in_1(in_1[7]), .in_2(in_2[7]), .in_3(substracter_7_out_5), .out_4(out_3[7]), .out_5(out_4));
endmodule

module half_adder (
  input  in_1,
  input  in_2,
  output out_3,
  output out_4
);

  xor xor_1 (out_3, in_1, in_2);
  and and_1 (out_4, in_1, in_2);
endmodule

module adder (
  input  in_1,
  input  in_2,
  input  in_3,
  output out_4,
  output out_5
);

  wire half_adder_1_out_3, half_adder_1_out_4, half_adder_2_out_4;

  half_adder half_adder_1 (.in_1(in_2), .in_2(in_3), .out_3(half_adder_1_out_3), .out_4(half_adder_1_out_4));
  half_adder half_adder_2 (.in_1(in_1), .in_2(half_adder_1_out_3), .out_3(out_4), .out_4(half_adder_2_out_4));
  or or_1 (out_5, half_adder_2_out_4, half_adder_1_out_4);
endmodule

module deMUX (
  input  in_1,
  input  [1:0] in_2,
  output out_3,
  output out_4,
  output out_5,
  output out_6
);

  wire and_1_out, not_1_out, not_2_out;

  not not_1 (not_1_out, in_2[0]);
  not not_2 (not_2_out, in_2[1]);
  and and_1 (and_1_out, not_1_out, not_2_out);
  and and_2 (out_3, in_1, and_1_out);
  buf and_3 (out_4, in_1);  // AND_Gate
  buf and_4 (out_5, in_1);  // AND_Gate
  buf and_5 (out_6, in_1);  // AND_Gate
endmodule

module adder_8_bit (
  input  [7:0] in_1,
  input  [7:0] in_2,
  output [7:0] out_3,
  output out_4
);

  wire adder_1_out_5, adder_2_out_5, adder_3_out_5, adder_4_out_5, adder_5_out_5, adder_6_out_5,
       adder_7_out_5;

  adder adder_1 (.in_1(in_1[0]), .in_2(in_2[0]), .in_3(1'b0), .out_4(out_3[0]), .out_5(adder_1_out_5));
  adder adder_2 (.in_1(in_1[1]), .in_2(in_2[1]), .in_3(adder_1_out_5), .out_4(out_3[1]), .out_5(adder_2_out_5));
  adder adder_3 (.in_1(in_1[2]), .in_2(in_2[2]), .in_3(adder_2_out_5), .out_4(out_3[2]), .out_5(adder_3_out_5));
  adder adder_4 (.in_1(in_1[3]), .in_2(in_2[3]), .in_3(adder_3_out_5), .out_4(out_3[3]), .out_5(adder_4_out_5));
  adder adder_5 (.in_1(in_1[4]), .in_2(in_2[4]), .in_3(adder_4_out_5), .out_4(out_3[4]), .out_5(adder_5_out_5));
  adder adder_6 (.in_1(in_1[5]), .in_2(in_2[5]), .in_3(adder_5_out_5), .out_4(out_3[5]), .out_5(adder_6_out_5));
  adder adder_7 (.in_1(in_1[6]), .in_2(in_2[6]), .in_3(adder_6_out_5), .out_4(out_3[6]), .out_5(adder_7_out_5));
  adder adder_8 (.in_1(in_1[7]), .in_2(in_2[7]), .in_3(adder_7_out_5), .out_4(out_3[7]), .out_5(out_4));
endmodule

module multiplyer (
  input  [7:0] in_1,
  input  [7:0] in_2,
  output [7:0] out_3,
  output [7:0] out_4
);

  wire adder_1_out_4, adder_2_out_4, adder_3_out_4, adder_4_out_4, adder_5_out_4, adder_6_out_4,
       adder_8_out_4, adder_8_out_5, adder_9_out_4, adder_9_out_5, adder_10_out_4, adder_10_out_5,
       adder_11_out_4, adder_11_out_5, adder_12_out_4, adder_12_out_5, adder_13_out_4, adder_13_out_5,
       adder_14_out_5, adder_15_out_4, adder_15_out_5, adder_16_out_4, adder_16_out_5, adder_17_out_4,
       adder_17_out_5, adder_18_out_4, adder_18_out_5, adder_19_out_4, adder_19_out_5, adder_20_out_4,
       adder_20_out_5, adder_21_out_5, adder_22_out_4, adder_22_out_5, adder_23_out_4, adder_23_out_5,
       adder_24_out_4, adder_24_out_5, adder_25_out_4, adder_25_out_5, adder_26_out_4, adder_26_out_5,
       adder_27_out_4, adder_27_out_5, adder_28_out_5, adder_29_out_4, adder_29_out_5, adder_30_out_4,
       adder_30_out_5, adder_31_out_4, adder_31_out_5, adder_32_out_4, adder_32_out_5, adder_33_out_4,
       adder_33_out_5, adder_34_out_4, adder_34_out_5, adder_35_out_5, adder_36_out_4, adder_36_out_5,
       adder_37_out_4, adder_37_out_5, adder_38_out_4, adder_38_out_5, adder_39_out_4, adder_39_out_5,
       adder_40_out_4, adder_40_out_5, adder_41_out_4, adder_41_out_5, adder_42_out_5, adder_43_out_4,
       adder_43_out_5, adder_44_out_4, adder_44_out_5, adder_45_out_4, adder_45_out_5, adder_46_out_4,
       adder_46_out_5, adder_47_out_4, adder_47_out_5, adder_48_out_4, adder_48_out_5, adder_49_out_5,
       adder_50_out_5, adder_51_out_5, adder_52_out_5, adder_53_out_5, adder_54_out_5, adder_55_out_5,
       adder_56_out_5, and_1_out, and_2_out, and_3_out, and_4_out, and_5_out, and_6_out, and_7_out,
       and_8_out, and_9_out, and_10_out, and_11_out, and_12_out, and_13_out, and_14_out, and_15_out,
       and_16_out, and_17_out, and_18_out, and_19_out, and_20_out, and_21_out, and_22_out, and_23_out,
       and_24_out, and_25_out, and_26_out, and_27_out, and_28_out, and_29_out, and_30_out, and_31_out,
       and_32_out, and_33_out, and_34_out, and_35_out, and_36_out, and_37_out, and_38_out, and_39_out,
       and_40_out, and_41_out, and_42_out, and_43_out, and_44_out, and_45_out, and_46_out, and_47_out,
       and_48_out, and_49_out, and_50_out, and_51_out, and_52_out, and_53_out, and_54_out, and_55_out,
       and_56_out, and_57_out, and_58_out, and_59_out, and_60_out, and_61_out, and_62_out, and_64_out;

  adder adder_1 (.in_1(and_1_out), .in_2(1'b0), .in_3(adder_8_out_5), .out_4(adder_1_out_4));  // open: out_5
  adder adder_2 (.in_1(and_2_out), .in_2(1'b0), .in_3(adder_9_out_5), .out_4(adder_2_out_4));  // open: out_5
  adder adder_3 (.in_1(and_3_out), .in_2(1'b0), .in_3(adder_10_out_5), .out_4(adder_3_out_4));  // open: out_5
  adder adder_4 (.in_1(and_4_out), .in_2(1'b0), .in_3(adder_11_out_5), .out_4(adder_4_out_4));  // open: out_5
  adder adder_5 (.in_1(and_5_out), .in_2(1'b0), .in_3(adder_12_out_5), .out_4(adder_5_out_4));  // open: out_5
  adder adder_6 (.in_1(and_6_out), .in_2(1'b0), .in_3(adder_13_out_5), .out_4(adder_6_out_4));  // open: out_5
  adder adder_7 (.in_1(and_7_out), .in_2(1'b0), .in_3(adder_14_out_5), .out_4(out_4[6]), .out_5(out_4[7]));
  and and_1 (and_1_out, in_1[7], in_2[1]);
  adder adder_8 (
    .in_1(and_8_out), .in_2(and_9_out), .in_3(adder_15_out_5), .out_4(adder_8_out_4), .out_5(adder_8_out_5));
  and and_2 (and_2_out, in_2[2], in_1[7]);
  adder adder_9 (
    .in_1(and_10_out), .in_2(adder_1_out_4), .in_3(adder_16_out_5), .out_4(adder_9_out_4),
    .out_5(adder_9_out_5));
  and and_3 (and_3_out, in_2[3], in_1[7]);
  adder adder_10 (
    .in_1(and_11_out), .in_2(adder_2_out_4), .in_3(adder_17_out_5), .out_4(adder_10_out_4),
    .out_5(adder_10_out_5));
  and and_4 (and_4_out, in_2[4], in_1[7]);
  adder adder_11 (
    .in_1(and_12_out), .in_2(adder_3_out_4), .in_3(adder_18_out_5), .out_4(adder_11_out_4),
    .out_5(adder_11_out_5));
  and and_5 (and_5_out, in_2[5], in_1[7]);
  adder adder_12 (
    .in_1(and_13_out), .in_2(adder_4_out_4), .in_3(adder_19_out_5), .out_4(adder_12_out_4),
    .out_5(adder_12_out_5));
  and and_6 (and_6_out, in_2[6], in_1[7]);
  adder adder_13 (
    .in_1(and_14_out), .in_2(adder_5_out_4), .in_3(adder_20_out_5), .out_4(adder_13_out_4),
    .out_5(adder_13_out_5));
  and and_7 (and_7_out, in_2[7], in_1[7]);
  adder adder_14 (
    .in_1(and_15_out), .in_2(adder_6_out_4), .in_3(adder_21_out_5), .out_4(out_4[5]), .out_5(adder_14_out_5));
  and and_8 (and_8_out, in_1[7], in_2[0]);
  and and_9 (and_9_out, in_1[6], in_2[1]);
  adder adder_15 (
    .in_1(and_16_out), .in_2(and_17_out), .in_3(adder_22_out_5), .out_4(adder_15_out_4),
    .out_5(adder_15_out_5));
  and and_10 (and_10_out, in_2[2], in_1[6]);
  adder adder_16 (
    .in_1(and_19_out), .in_2(adder_8_out_4), .in_3(adder_23_out_5), .out_4(adder_16_out_4),
    .out_5(adder_16_out_5));
  and and_11 (and_11_out, in_2[3], in_1[6]);
  adder adder_17 (
    .in_1(and_21_out), .in_2(adder_9_out_4), .in_3(adder_24_out_5), .out_4(adder_17_out_4),
    .out_5(adder_17_out_5));
  and and_12 (and_12_out, in_2[4], in_1[6]);
  adder adder_18 (
    .in_1(and_22_out), .in_2(adder_10_out_4), .in_3(adder_25_out_5), .out_4(adder_18_out_4),
    .out_5(adder_18_out_5));
  and and_13 (and_13_out, in_2[5], in_1[6]);
  adder adder_19 (
    .in_1(and_24_out), .in_2(adder_11_out_4), .in_3(adder_26_out_5), .out_4(adder_19_out_4),
    .out_5(adder_19_out_5));
  and and_14 (and_14_out, in_2[6], in_1[6]);
  adder adder_20 (
    .in_1(and_26_out), .in_2(adder_12_out_4), .in_3(adder_27_out_5), .out_4(adder_20_out_4),
    .out_5(adder_20_out_5));
  and and_15 (and_15_out, in_2[7], in_1[6]);
  adder adder_21 (
    .in_1(and_29_out), .in_2(adder_13_out_4), .in_3(adder_28_out_5), .out_4(out_4[4]), .out_5(adder_21_out_5));
  and and_16 (and_16_out, in_1[6], in_2[0]);
  and and_17 (and_17_out, in_1[5], in_2[1]);
  adder adder_22 (
    .in_1(and_31_out), .in_2(and_33_out), .in_3(adder_29_out_5), .out_4(adder_22_out_4),
    .out_5(adder_22_out_5));
  and and_18 (and_18_out, in_2[2], in_1[4]);
  and and_19 (and_19_out, in_2[2], in_1[5]);
  adder adder_23 (
    .in_1(and_18_out), .in_2(adder_15_out_4), .in_3(adder_30_out_5), .out_4(adder_23_out_4),
    .out_5(adder_23_out_5));
  and and_20 (and_20_out, in_2[3], in_1[4]);
  and and_21 (and_21_out, in_2[3], in_1[5]);
  adder adder_24 (
    .in_1(and_20_out), .in_2(adder_16_out_4), .in_3(adder_31_out_5), .out_4(adder_24_out_4),
    .out_5(adder_24_out_5));
  and and_22 (and_22_out, in_2[4], in_1[5]);
  and and_23 (and_23_out, in_2[4], in_1[4]);
  adder adder_25 (
    .in_1(and_23_out), .in_2(adder_17_out_4), .in_3(adder_32_out_5), .out_4(adder_25_out_4),
    .out_5(adder_25_out_5));
  and and_24 (and_24_out, in_2[5], in_1[5]);
  and and_25 (and_25_out, in_2[5], in_1[4]);
  adder adder_26 (
    .in_1(and_25_out), .in_2(adder_18_out_4), .in_3(adder_33_out_5), .out_4(adder_26_out_4),
    .out_5(adder_26_out_5));
  and and_26 (and_26_out, in_2[6], in_1[5]);
  and and_27 (and_27_out, in_2[6], in_1[4]);
  adder adder_27 (
    .in_1(and_27_out), .in_2(adder_19_out_4), .in_3(adder_34_out_5), .out_4(adder_27_out_4),
    .out_5(adder_27_out_5));
  and and_28 (and_28_out, in_2[7], in_1[4]);
  and and_29 (and_29_out, in_2[7], in_1[5]);
  adder adder_28 (
    .in_1(and_28_out), .in_2(adder_20_out_4), .in_3(adder_35_out_5), .out_4(out_4[3]), .out_5(adder_28_out_5));
  and and_30 (and_30_out, in_1[4], in_2[0]);
  and and_31 (and_31_out, in_1[5], in_2[0]);
  and and_32 (and_32_out, in_1[3], in_2[1]);
  and and_33 (and_33_out, in_1[4], in_2[1]);
  adder adder_29 (
    .in_1(and_30_out), .in_2(and_32_out), .in_3(adder_36_out_5), .out_4(adder_29_out_4),
    .out_5(adder_29_out_5));
  and and_34 (and_34_out, in_2[2], in_1[3]);
  adder adder_30 (
    .in_1(and_34_out), .in_2(adder_22_out_4), .in_3(adder_37_out_5), .out_4(adder_30_out_4),
    .out_5(adder_30_out_5));
  and and_35 (and_35_out, in_2[3], in_1[3]);
  adder adder_31 (
    .in_1(and_35_out), .in_2(adder_23_out_4), .in_3(adder_38_out_5), .out_4(adder_31_out_4),
    .out_5(adder_31_out_5));
  and and_36 (and_36_out, in_2[4], in_1[3]);
  adder adder_32 (
    .in_1(and_36_out), .in_2(adder_24_out_4), .in_3(adder_39_out_5), .out_4(adder_32_out_4),
    .out_5(adder_32_out_5));
  and and_37 (and_37_out, in_2[5], in_1[3]);
  adder adder_33 (
    .in_1(and_37_out), .in_2(adder_25_out_4), .in_3(adder_40_out_5), .out_4(adder_33_out_4),
    .out_5(adder_33_out_5));
  and and_38 (and_38_out, in_2[6], in_1[3]);
  adder adder_34 (
    .in_1(and_38_out), .in_2(adder_26_out_4), .in_3(adder_41_out_5), .out_4(adder_34_out_4),
    .out_5(adder_34_out_5));
  and and_39 (and_39_out, in_2[7], in_1[3]);
  adder adder_35 (
    .in_1(and_39_out), .in_2(adder_27_out_4), .in_3(adder_42_out_5), .out_4(out_4[2]), .out_5(adder_35_out_5));
  and and_40 (and_40_out, in_1[3], in_2[0]);
  and and_41 (and_41_out, in_1[2], in_2[1]);
  adder adder_36 (
    .in_1(and_40_out), .in_2(and_41_out), .in_3(adder_43_out_5), .out_4(adder_36_out_4),
    .out_5(adder_36_out_5));
  and and_42 (and_42_out, in_2[2], in_1[2]);
  adder adder_37 (
    .in_1(and_42_out), .in_2(adder_29_out_4), .in_3(adder_44_out_5), .out_4(adder_37_out_4),
    .out_5(adder_37_out_5));
  and and_43 (and_43_out, in_2[3], in_1[2]);
  adder adder_38 (
    .in_1(and_43_out), .in_2(adder_30_out_4), .in_3(adder_45_out_5), .out_4(adder_38_out_4),
    .out_5(adder_38_out_5));
  and and_44 (and_44_out, in_2[4], in_1[2]);
  adder adder_39 (
    .in_1(and_44_out), .in_2(adder_31_out_4), .in_3(adder_46_out_5), .out_4(adder_39_out_4),
    .out_5(adder_39_out_5));
  and and_45 (and_45_out, in_2[5], in_1[2]);
  adder adder_40 (
    .in_1(and_45_out), .in_2(adder_32_out_4), .in_3(adder_47_out_5), .out_4(adder_40_out_4),
    .out_5(adder_40_out_5));
  and and_46 (and_46_out, in_2[6], in_1[2]);
  adder adder_41 (
    .in_1(and_46_out), .in_2(adder_33_out_4), .in_3(adder_48_out_5), .out_4(adder_41_out_4),
    .out_5(adder_41_out_5));
  and and_47 (and_47_out, in_2[7], in_1[2]);
  adder adder_42 (
    .in_1(and_47_out), .in_2(adder_34_out_4), .in_3(adder_49_out_5), .out_4(out_4[1]), .out_5(adder_42_out_5));
  and and_48 (and_48_out, in_1[2], in_2[0]);
  and and_49 (and_49_out, in_1[1], in_2[1]);
  adder adder_43 (
    .in_1(and_48_out), .in_2(and_49_out), .in_3(adder_50_out_5), .out_4(adder_43_out_4),
    .out_5(adder_43_out_5));
  and and_50 (and_50_out, in_2[2], in_1[0]);
  and and_51 (and_51_out, in_2[2], in_1[1]);
  adder adder_44 (
    .in_1(and_51_out), .in_2(adder_36_out_4), .in_3(adder_51_out_5), .out_4(adder_44_out_4),
    .out_5(adder_44_out_5));
  and and_52 (and_52_out, in_2[3], in_1[0]);
  and and_53 (and_53_out, in_2[3], in_1[1]);
  adder adder_45 (
    .in_1(and_53_out), .in_2(adder_37_out_4), .in_3(adder_52_out_5), .out_4(adder_45_out_4),
    .out_5(adder_45_out_5));
  and and_54 (and_54_out, in_2[4], in_1[0]);
  and and_55 (and_55_out, in_2[4], in_1[1]);
  adder adder_46 (
    .in_1(and_55_out), .in_2(adder_38_out_4), .in_3(adder_53_out_5), .out_4(adder_46_out_4),
    .out_5(adder_46_out_5));
  and and_56 (and_56_out, in_2[5], in_1[1]);
  and and_57 (and_57_out, in_2[5], in_1[0]);
  adder adder_47 (
    .in_1(and_56_out), .in_2(adder_39_out_4), .in_3(adder_54_out_5), .out_4(adder_47_out_4),
    .out_5(adder_47_out_5));
  and and_58 (and_58_out, in_2[6], in_1[1]);
  and and_59 (and_59_out, in_2[6], in_1[0]);
  adder adder_48 (
    .in_1(and_58_out), .in_2(adder_40_out_4), .in_3(adder_55_out_5), .out_4(adder_48_out_4),
    .out_5(adder_48_out_5));
  and and_60 (and_60_out, in_2[7], in_1[1]);
  and and_61 (and_61_out, in_2[7], in_1[0]);
  adder adder_49 (
    .in_1(and_60_out), .in_2(adder_41_out_4), .in_3(adder_56_out_5), .out_4(out_4[0]), .out_5(adder_49_out_5));
  and and_62 (and_62_out, in_1[1], in_2[0]);
  and and_63 (out_3[0], in_1[0], in_2[0]);
  and and_64 (and_64_out, in_1[0], in_2[1]);
  adder adder_50 (.in_1(and_62_out), .in_2(and_64_out), .in_3(1'b0), .out_4(out_3[1]), .out_5(adder_50_out_5));
  adder adder_51 (.in_1(and_50_out), .in_2(adder_43_out_4), .in_3(1'b0), .out_4(out_3[2]), .out_5(adder_51_out_5));
  adder adder_52 (.in_1(and_52_out), .in_2(adder_44_out_4), .in_3(1'b0), .out_4(out_3[3]), .out_5(adder_52_out_5));
  adder adder_53 (.in_1(and_54_out), .in_2(adder_45_out_4), .in_3(1'b0), .out_4(out_3[4]), .out_5(adder_53_out_5));
  adder adder_54 (.in_1(and_57_out), .in_2(adder_46_out_4), .in_3(1'b0), .out_4(out_3[5]), .out_5(adder_54_out_5));
  adder adder_55 (.in_1(and_59_out), .in_2(adder_47_out_4), .in_3(1'b0), .out_4(out_3[6]), .out_5(adder_55_out_5));
  adder adder_56 (.in_1(and_61_out), .in_2(adder_48_out_4), .in_3(1'b0), .out_4(out_3[7]), .out_5(adder_56_out_5));

  // Other names for the same wires on the sheet: _8 = in_1[0]; _7 = in_1[1]; _6 = in_1[2]; _5 = in_1[3]; _4 = in_1[4];
  //   _3 = in_1[5]; _2 = in_1[6]; _1 = in_1[7]
endmodule

module adder_8_bit_signed (
  input  [7:0] in_1,
  input  [7:0] in_2,
  output [7:0] out_3,
  output S
);

  wire adder_1_out_5, adder_2_out_5, adder_3_out_5, adder_4_out_5, adder_5_out_5, adder_6_out_5,
       adder_7_out_5, adder_8_out_5;

  adder adder_1 (.in_1(in_1[0]), .in_2(in_2[0]), .in_3(1'b0), .out_4(out_3[0]), .out_5(adder_1_out_5));
  adder adder_2 (.in_1(in_1[1]), .in_2(in_2[1]), .in_3(adder_1_out_5), .out_4(out_3[1]), .out_5(adder_2_out_5));
  adder adder_3 (.in_1(in_1[2]), .in_2(in_2[2]), .in_3(adder_2_out_5), .out_4(out_3[2]), .out_5(adder_3_out_5));
  adder adder_4 (.in_1(in_1[3]), .in_2(in_2[3]), .in_3(adder_3_out_5), .out_4(out_3[3]), .out_5(adder_4_out_5));
  adder adder_5 (.in_1(in_1[4]), .in_2(in_2[4]), .in_3(adder_4_out_5), .out_4(out_3[4]), .out_5(adder_5_out_5));
  adder adder_6 (.in_1(in_1[5]), .in_2(in_2[5]), .in_3(adder_5_out_5), .out_4(out_3[5]), .out_5(adder_6_out_5));
  adder adder_7 (.in_1(in_1[6]), .in_2(in_2[6]), .in_3(adder_6_out_5), .out_4(out_3[6]), .out_5(adder_7_out_5));
  adder adder_8 (.in_1(in_1[7]), .in_2(in_2[7]), .in_3(adder_7_out_5), .out_4(out_3[7]), .out_5(adder_8_out_5));
  xor xor_1 (S, adder_8_out_5, adder_7_out_5);
endmodule

module substracter_8_bit_signed (
  input  [7:0] in_1,
  input  [7:0] in_2,
  output [7:0] out_3,
  output out_4
);

  wire substracter_1_out_5, substracter_2_out_5, substracter_3_out_5, substracter_4_out_5,
       substracter_5_out_5, substracter_6_out_5, substracter_7_out_5;

  substracter substracter_1 (
    .in_1(in_1[0]), .in_2(in_2[0]), .in_3(1'b0), .out_4(out_3[0]), .out_5(substracter_1_out_5));
  substracter substracter_2 (
    .in_1(in_1[1]), .in_2(in_2[1]), .in_3(substracter_1_out_5), .out_4(out_3[1]), .out_5(substracter_2_out_5));
  substracter substracter_3 (
    .in_1(in_1[2]), .in_2(in_2[2]), .in_3(substracter_2_out_5), .out_4(out_3[2]), .out_5(substracter_3_out_5));
  substracter substracter_4 (
    .in_1(in_1[3]), .in_2(in_2[3]), .in_3(substracter_3_out_5), .out_4(out_3[3]), .out_5(substracter_4_out_5));
  substracter substracter_5 (
    .in_1(in_1[4]), .in_2(in_2[4]), .in_3(substracter_4_out_5), .out_4(out_3[4]), .out_5(substracter_5_out_5));
  substracter substracter_6 (
    .in_1(in_1[5]), .in_2(in_2[5]), .in_3(substracter_5_out_5), .out_4(out_3[5]), .out_5(substracter_6_out_5));
  substracter substracter_7 (
    .in_1(in_1[6]), .in_2(in_2[6]), .in_3(substracter_6_out_5), .out_4(out_3[6]), .out_5(substracter_7_out_5));
  substracter substracter_8 (
    .in_1(in_1[7]), .in_2(in_2[7]), .in_3(substracter_7_out_5), .out_4(out_3[7]), .out_5(out_4));
endmodule

module multiply_4_bit (
  input  [3:0] D,
  input  [3:0] \С ,
  input  [3:0] in_3,
  input  [3:0] in_4,
  output [3:0] out_5,
  output [3:0] out_6
);

  wire adder_1_out_4, adder_1_out_5, adder_2_out_4, adder_2_out_5, adder_3_out_4, adder_3_out_5,
       adder_4_out_4, adder_4_out_5, adder_5_out_4, adder_5_out_5, adder_6_out_4, adder_6_out_5,
       adder_7_out_4, adder_7_out_5, adder_8_out_4, adder_8_out_5, adder_9_out_4, adder_9_out_5,
       adder_10_out_5, adder_11_out_5, adder_12_out_5, adder_13_out_5, adder_14_out_5, adder_15_out_5,
       and_1_out, and_2_out, and_3_out, and_4_out, and_5_out, and_6_out, and_7_out, and_8_out, and_9_out,
       and_10_out, and_11_out, and_12_out, and_13_out, and_14_out, and_15_out, and_16_out;

  and and_1 (and_1_out, in_3[0], in_4[0]);
  and and_2 (and_2_out, in_3[1], in_4[0]);
  and and_3 (and_3_out, in_3[0], in_4[1]);
  and and_4 (and_4_out, in_3[1], in_4[1]);
  and and_5 (and_5_out, in_3[2], in_4[0]);
  and and_6 (and_6_out, in_4[0], in_3[3]);
  and and_7 (and_7_out, in_4[1], in_3[2]);
  and and_8 (and_8_out, in_3[1], in_4[2]);
  and and_9 (and_9_out, in_3[3], in_4[1]);
  and and_10 (and_10_out, in_3[3], in_4[2]);
  and and_11 (and_11_out, in_3[2], in_4[3]);
  and and_12 (and_12_out, in_3[3], in_4[3]);
  adder adder_1 (.in_1(and_2_out), .in_2(and_3_out), .in_3(\С [1]), .out_4(adder_1_out_4), .out_5(adder_1_out_5));
  and and_13 (and_13_out, in_3[0], in_4[2]);
  and and_14 (and_14_out, in_3[0], in_4[3]);
  and and_15 (and_15_out, in_3[2], in_4[2]);
  and and_16 (and_16_out, in_4[3], in_3[1]);
  adder adder_2 (.in_1(and_4_out), .in_2(and_5_out), .in_3(\С [2]), .out_4(adder_2_out_4), .out_5(adder_2_out_5));
  adder adder_3 (.in_1(and_6_out), .in_2(and_7_out), .in_3(\С [3]), .out_4(adder_3_out_4), .out_5(adder_3_out_5));
  adder adder_4 (
    .in_1(and_9_out), .in_2(and_15_out), .in_3(adder_3_out_5), .out_4(adder_4_out_4), .out_5(adder_4_out_5));
  adder adder_5 (
    .in_1(adder_2_out_4), .in_2(adder_1_out_5), .in_3(and_13_out), .out_4(adder_5_out_4),
    .out_5(adder_5_out_5));
  adder adder_6 (
    .in_1(and_10_out), .in_2(and_11_out), .in_3(adder_4_out_5), .out_4(adder_6_out_4), .out_5(adder_6_out_5));
  adder adder_7 (
    .in_1(adder_3_out_4), .in_2(and_8_out), .in_3(adder_2_out_5), .out_4(adder_7_out_4), .out_5(adder_7_out_5));
  adder adder_8 (
    .in_1(adder_4_out_4), .in_2(and_16_out), .in_3(adder_7_out_5), .out_4(adder_8_out_4),
    .out_5(adder_8_out_5));
  adder adder_9 (
    .in_1(adder_7_out_4), .in_2(and_14_out), .in_3(adder_5_out_5), .out_4(adder_9_out_4),
    .out_5(adder_9_out_5));
  adder adder_10 (.in_1(and_1_out), .in_2(\С [0]), .in_3(D[0]), .out_4(out_5[0]), .out_5(adder_10_out_5));
  adder adder_11 (.in_1(D[1]), .in_2(adder_1_out_4), .in_3(adder_10_out_5), .out_4(out_5[1]), .out_5(adder_11_out_5));
  adder adder_12 (.in_1(adder_5_out_4), .in_2(D[2]), .in_3(adder_11_out_5), .out_4(out_5[2]), .out_5(adder_12_out_5));
  adder adder_13 (.in_1(D[3]), .in_2(adder_9_out_4), .in_3(adder_12_out_5), .out_4(out_5[3]), .out_5(adder_13_out_5));
  adder adder_14 (
    .in_1(adder_9_out_5), .in_2(adder_8_out_4), .in_3(adder_13_out_5), .out_4(out_6[0]),
    .out_5(adder_14_out_5));
  adder adder_15 (
    .in_1(adder_8_out_5), .in_2(adder_6_out_4), .in_3(adder_14_out_5), .out_4(out_6[1]),
    .out_5(adder_15_out_5));
  adder adder_16 (.in_1(adder_6_out_5), .in_2(and_12_out), .in_3(adder_15_out_5), .out_4(out_6[2]), .out_5(out_6[3]));
endmodule

module multiply_8_bit (
  input  [7:0] A,
  input  [7:0] B,
  output [7:0] M,
  output [7:0] C
);

  wire [3:0] multiply_4_bit_1_out_5, multiply_4_bit_1_out_6, multiply_4_bit_2_out_6, multiply_4_bit_3_out_6;

  multiply_4_bit multiply_4_bit_1 (
    .in_3(A[3:0]), .in_4(B[7:4]), .\С (4'b0000), .D(4'b0000), .out_5(multiply_4_bit_1_out_5),
    .out_6(multiply_4_bit_1_out_6));
  multiply_4_bit multiply_4_bit_2 (
    .in_3(A[3:0]), .in_4(B[3:0]), .\С (4'b0000), .D(4'b0000), .out_5(M[3:0]), .out_6(multiply_4_bit_2_out_6));
  multiply_4_bit multiply_4_bit_3 (
    .in_3(A[7:4]), .in_4(B[3:0]), .\С (multiply_4_bit_2_out_6), .D(multiply_4_bit_1_out_5), .out_5(M[7:4]),
    .out_6(multiply_4_bit_3_out_6));
  multiply_4_bit multiply_4_bit_4 (
    .in_3(A[7:4]), .in_4(B[7:4]), .\С (multiply_4_bit_1_out_6), .D(multiply_4_bit_3_out_6), .out_5(C[3:0]),
    .out_6(C[7:4]));
endmodule

module division_8_bit (
  input  [7:0] A,
  input  [7:0] D,
  output [7:0] Q,
  output Err
);

  wire not_2_out_2, not_3_out_2, not_4_out_2, not_5_out_2, not_6_out_2, not_7_out_2, not_8_out_2,
       not_9_out_2, unsigned_1_out_3, unsigned_2_out_3, unsigned_3_out_3, unsigned_4_out_3, unsigned_5_out_3,
       unsigned_6_out_3, unsigned_7_out_3, unsigned_8_out_3;
  wire [7:0] multiplier_1_cout, multiplier_1_out, multiplier_2_cout, multiplier_2_out, multiplier_3_cout,
       multiplier_3_out, multiplier_4_cout, multiplier_4_out, multiplier_5_cout, multiplier_5_out,
       multiplier_6_cout, multiplier_6_out, multiplier_7_cout, multiplier_7_out, multiplier_8_cout,
       multiplier_8_out;

  NOT not_1 (.in_1(D), .out_2(Err));
  \unsigned  unsigned_1 (.in_1(A), .in_2(multiplier_1_out), .out_3(unsigned_1_out_3));
  Multiplier multiplier_1 (.a(D), .b(8'h80), .out(multiplier_1_out), .cout(multiplier_1_cout));  // open: cin
  and and_1 (Q[7], unsigned_1_out_3, not_2_out_2);
  NOT not_2 (.in_1(multiplier_1_cout), .out_2(not_2_out_2));
  \unsigned  unsigned_2 (.in_1(A), .in_2(multiplier_2_out), .out_3(unsigned_2_out_3));
  Multiplier multiplier_2 (
    .a(D), .b({Q[7], 7'b1000000}), .out(multiplier_2_out), .cout(multiplier_2_cout));  // open: cin
  and and_2 (Q[6], unsigned_2_out_3, not_3_out_2);
  NOT not_3 (.in_1(multiplier_2_cout), .out_2(not_3_out_2));
  Multiplier multiplier_3 (
    .a(D), .b({Q[7:6], 6'b100000}), .out(multiplier_3_out), .cout(multiplier_3_cout));  // open: cin
  NOT not_4 (.in_1(multiplier_3_cout), .out_2(not_4_out_2));
  and and_3 (Q[5], not_4_out_2, unsigned_3_out_3);
  \unsigned  unsigned_3 (.in_1(A), .in_2(multiplier_3_out), .out_3(unsigned_3_out_3));
  \unsigned  unsigned_4 (.in_1(A), .in_2(multiplier_4_out), .out_3(unsigned_4_out_3));
  NOT not_5 (.in_1(multiplier_4_cout), .out_2(not_5_out_2));
  Multiplier multiplier_4 (
    .a(D), .b({Q[7:5], 5'b10000}), .out(multiplier_4_out), .cout(multiplier_4_cout));  // open: cin
  and and_4 (Q[4], unsigned_4_out_3, not_5_out_2);
  \unsigned  unsigned_5 (.in_1(A), .in_2(multiplier_5_out), .out_3(unsigned_5_out_3));
  Multiplier multiplier_5 (
    .a(D), .b({Q[7:4], 4'b1000}), .out(multiplier_5_out), .cout(multiplier_5_cout));  // open: cin
  and and_5 (Q[3], unsigned_5_out_3, not_6_out_2);
  NOT not_6 (.in_1(multiplier_5_cout), .out_2(not_6_out_2));
  Multiplier multiplier_6 (.a(D), .b({Q[7:3], 3'b100}), .out(multiplier_6_out), .cout(multiplier_6_cout));  // open: cin
  \unsigned  unsigned_6 (.in_1(A), .in_2(multiplier_6_out), .out_3(unsigned_6_out_3));
  Multiplier multiplier_7 (.a(D), .b({Q[7:2], 2'b10}), .out(multiplier_7_out), .cout(multiplier_7_cout));  // open: cin
  and and_6 (Q[2], unsigned_6_out_3, not_7_out_2);
  NOT not_7 (.in_1(multiplier_6_cout), .out_2(not_7_out_2));
  \unsigned  unsigned_7 (.in_1(A), .in_2(multiplier_7_out), .out_3(unsigned_7_out_3));
  and and_7 (Q[1], unsigned_7_out_3, not_8_out_2);
  NOT not_8 (.in_1(multiplier_7_cout), .out_2(not_8_out_2));
  Multiplier multiplier_8 (.a(D), .b({Q[7:1], 1'b1}), .out(multiplier_8_out), .cout(multiplier_8_cout));  // open: cin
  \unsigned  unsigned_8 (.in_1(A), .in_2(multiplier_8_out), .out_3(unsigned_8_out_3));
  NOT not_9 (.in_1(multiplier_8_cout), .out_2(not_9_out_2));
  and and_8 (Q[0], unsigned_8_out_3, not_9_out_2);
endmodule

module convert_straight (
  input  [7:0] in_1,
  output [7:0] out_2
);

  wire [7:0] not_1_out, subtractor_1_out;

  Subtractor subtractor_1 (.a(in_1), .b(8'h1), .out(subtractor_1_out));  // open: bin, bout
  assign not_1_out = ~subtractor_1_out;  // NOT_Gate not_1, 8 bits wide
  Multiplexer #(.width(8)) multiplexer_1 (.in0(in_1), .in1(not_1_out), .out(out_2), .sel(in_1[7]));  // open: en
endmodule

module division_8_bit_unsigned (
  input  [7:0] in_1,
  input  [7:0] in_2,
  output [7:0] R
);

  wire xor_1_out;
  wire [7:0] adder_1_out, convert_straight_1_out_2, convert_straight_2_out_2, division_8_bit_1_q, not_1_out;

  convert_straight convert_straight_1 (.in_1(in_1), .out_2(convert_straight_1_out_2));
  convert_straight convert_straight_2 (.in_1(in_2), .out_2(convert_straight_2_out_2));
  xor xor_1 (xor_1_out, in_1[7], in_2[7]);
  division_8_bit division_8_bit_1 (
    .A(convert_straight_1_out_2), .D(convert_straight_2_out_2), .Q(division_8_bit_1_q));  // open: Err
  assign not_1_out = ~division_8_bit_1_q;  // NOT_Gate not_1, 8 bits wide
  Multiplexer #(.width(8)) multiplexer_1 (
    .in0(division_8_bit_1_q), .in1(adder_1_out), .out(R), .sel(xor_1_out));  // open: en
  Adder adder_1 (.a(not_1_out), .b(8'h1), .out(adder_1_out));  // open: cin, cout
endmodule

module stolbikk (
  input  [7:0] in_1,
  input  [7:0] in_2,
  output [7:0] out_3,
  output [7:0] out_4,
  output out_5,
  output out_6
);

  wire not_1_out, not_2_out;
  wire [2:0] register_3_q;
  wire [7:0] multiplexer_1_out, multiplexer_2_out, register_1_q, register_2_q;

  Register register_1 (.Q(register_1_q));  // open: D, en, clk, clr
  Multiplexer #(.width(8)) multiplexer_1 (
    .in0(in_1), .in1(register_1_q), .out(multiplexer_1_out), .sel(not_1_out));  // open: en
  assign out_3 = multiplexer_1_out;  // Buffer buffer_1, 8 bits wide
  not not_1 (not_1_out, in_2[0]);
  Register register_2 (.Q(register_2_q));  // open: D, en, clk, clr
  not not_2 (not_2_out, in_2[1]);
  Bit_Extender #(.in_width(1), .out_width(3)) bit_extender_1 ();  // open: in, out
  Register #(.width(3)) register_3 (.Q(register_3_q));  // open: D, en, clk, clr
  arifmetical_shl arifmetical_shl_1 (.in_1(register_3_q), .in_2(multiplexer_2_out), .out_3(out_4), .out_4(out_5));
  Multiplexer #(.width(8)) multiplexer_2 (
    .in0(in_1), .in1(register_2_q), .out(multiplexer_2_out), .sel(not_2_out));  // open: en
  arifmetical_shl arifmetical_shl_2 (.out_4(out_6));  // open: in_1, in_2, out_3

  // Other names for the same wires on the sheet: _1[7:0] = in_1
endmodule

module multiplyer2 (
  input  [7:0] in_1,
  input  [7:0] in_2,
  output [7:0] out_3,
  output [7:0] out_4
);

  wire adder_1_out_4, adder_2_out_4, adder_3_out_4, adder_4_out_4, adder_5_out_4, adder_6_out_4,
       adder_8_out_4, adder_8_out_5, adder_9_out_4, adder_9_out_5, adder_10_out_4, adder_10_out_5,
       adder_11_out_4, adder_11_out_5, adder_12_out_4, adder_12_out_5, adder_13_out_4, adder_13_out_5,
       adder_14_out_5, adder_15_out_4, adder_15_out_5, adder_16_out_4, adder_16_out_5, adder_17_out_4,
       adder_17_out_5, adder_18_out_4, adder_18_out_5, adder_19_out_4, adder_19_out_5, adder_20_out_4,
       adder_20_out_5, adder_21_out_5, adder_22_out_4, adder_22_out_5, adder_23_out_4, adder_23_out_5,
       adder_24_out_4, adder_24_out_5, adder_25_out_4, adder_25_out_5, adder_26_out_4, adder_26_out_5,
       adder_27_out_4, adder_27_out_5, adder_28_out_5, adder_29_out_4, adder_29_out_5, adder_30_out_4,
       adder_30_out_5, adder_31_out_4, adder_31_out_5, adder_32_out_4, adder_32_out_5, adder_33_out_4,
       adder_33_out_5, adder_34_out_4, adder_34_out_5, adder_35_out_5, adder_36_out_4, adder_36_out_5,
       adder_37_out_4, adder_37_out_5, adder_38_out_4, adder_38_out_5, adder_39_out_4, adder_39_out_5,
       adder_40_out_4, adder_40_out_5, adder_41_out_4, adder_41_out_5, adder_42_out_5, adder_43_out_4,
       adder_43_out_5, adder_44_out_4, adder_44_out_5, adder_45_out_4, adder_45_out_5, adder_46_out_4,
       adder_46_out_5, adder_47_out_4, adder_47_out_5, adder_48_out_4, adder_48_out_5, adder_49_out_5,
       adder_50_out_5, adder_51_out_5, adder_52_out_5, adder_53_out_5, adder_54_out_5, adder_55_out_5,
       adder_56_out_5, and_1_out, and_2_out, and_3_out, and_4_out, and_5_out, and_6_out, and_7_out,
       and_8_out, and_9_out, and_10_out, and_11_out, and_12_out, and_13_out, and_14_out, and_15_out,
       and_16_out, and_17_out, and_18_out, and_19_out, and_20_out, and_21_out, and_22_out, and_23_out,
       and_24_out, and_25_out, and_26_out, and_27_out, and_28_out, and_29_out, and_30_out, and_31_out,
       and_32_out, and_33_out, and_34_out, and_35_out, and_36_out, and_37_out, and_38_out, and_39_out,
       and_40_out, and_41_out, and_42_out, and_43_out, and_44_out, and_45_out, and_46_out, and_47_out,
       and_48_out, and_49_out, and_50_out, and_51_out, and_52_out, and_53_out, and_54_out, and_55_out,
       and_56_out, and_57_out, and_58_out, and_59_out, and_60_out, and_61_out, and_63_out, and_64_out;

  adder adder_1 (.in_1(and_1_out), .in_2(1'b0), .in_3(adder_8_out_5), .out_4(adder_1_out_4));  // open: out_5
  adder adder_2 (.in_1(and_2_out), .in_2(1'b0), .in_3(adder_9_out_5), .out_4(adder_2_out_4));  // open: out_5
  adder adder_3 (.in_1(and_3_out), .in_2(1'b0), .in_3(adder_10_out_5), .out_4(adder_3_out_4));  // open: out_5
  adder adder_4 (.in_1(and_4_out), .in_2(1'b0), .in_3(adder_11_out_5), .out_4(adder_4_out_4));  // open: out_5
  adder adder_5 (.in_1(and_5_out), .in_2(1'b0), .in_3(adder_12_out_5), .out_4(adder_5_out_4));  // open: out_5
  adder adder_6 (.in_1(and_6_out), .in_2(1'b0), .in_3(adder_13_out_5), .out_4(adder_6_out_4));  // open: out_5
  adder adder_7 (.in_1(and_7_out), .in_2(1'b0), .in_3(adder_14_out_5), .out_4(out_4[6]), .out_5(out_4[7]));
  and and_1 (and_1_out, in_1[7], in_2[1]);
  adder adder_8 (
    .in_1(and_8_out), .in_2(and_9_out), .in_3(adder_15_out_5), .out_4(adder_8_out_4), .out_5(adder_8_out_5));
  and and_2 (and_2_out, in_2[2], in_1[7]);
  adder adder_9 (
    .in_1(and_10_out), .in_2(adder_1_out_4), .in_3(adder_16_out_5), .out_4(adder_9_out_4),
    .out_5(adder_9_out_5));
  and and_3 (and_3_out, in_2[3], in_1[7]);
  adder adder_10 (
    .in_1(and_11_out), .in_2(adder_2_out_4), .in_3(adder_17_out_5), .out_4(adder_10_out_4),
    .out_5(adder_10_out_5));
  and and_4 (and_4_out, in_2[4], in_1[7]);
  adder adder_11 (
    .in_1(and_12_out), .in_2(adder_3_out_4), .in_3(adder_18_out_5), .out_4(adder_11_out_4),
    .out_5(adder_11_out_5));
  and and_5 (and_5_out, in_2[5], in_1[7]);
  adder adder_12 (
    .in_1(and_13_out), .in_2(adder_4_out_4), .in_3(adder_19_out_5), .out_4(adder_12_out_4),
    .out_5(adder_12_out_5));
  and and_6 (and_6_out, in_2[6], in_1[7]);
  adder adder_13 (
    .in_1(and_14_out), .in_2(adder_5_out_4), .in_3(adder_20_out_5), .out_4(adder_13_out_4),
    .out_5(adder_13_out_5));
  and and_7 (and_7_out, in_2[7], in_1[7]);
  adder adder_14 (
    .in_1(and_15_out), .in_2(adder_6_out_4), .in_3(adder_21_out_5), .out_4(out_4[5]), .out_5(adder_14_out_5));
  and and_8 (and_8_out, in_1[7], in_2[0]);
  and and_9 (and_9_out, in_1[6], in_2[1]);
  adder adder_15 (
    .in_1(and_16_out), .in_2(and_17_out), .in_3(adder_22_out_5), .out_4(adder_15_out_4),
    .out_5(adder_15_out_5));
  and and_10 (and_10_out, in_2[2], in_1[6]);
  adder adder_16 (
    .in_1(and_18_out), .in_2(adder_8_out_4), .in_3(adder_23_out_5), .out_4(adder_16_out_4),
    .out_5(adder_16_out_5));
  and and_11 (and_11_out, in_2[3], in_1[6]);
  adder adder_17 (
    .in_1(and_21_out), .in_2(adder_9_out_4), .in_3(adder_24_out_5), .out_4(adder_17_out_4),
    .out_5(adder_17_out_5));
  and and_12 (and_12_out, in_2[4], in_1[6]);
  adder adder_18 (
    .in_1(and_23_out), .in_2(adder_10_out_4), .in_3(adder_25_out_5), .out_4(adder_18_out_4),
    .out_5(adder_18_out_5));
  and and_13 (and_13_out, in_2[5], in_1[6]);
  adder adder_19 (
    .in_1(and_25_out), .in_2(adder_11_out_4), .in_3(adder_26_out_5), .out_4(adder_19_out_4),
    .out_5(adder_19_out_5));
  and and_14 (and_14_out, in_2[6], in_1[6]);
  adder adder_20 (
    .in_1(and_27_out), .in_2(adder_12_out_4), .in_3(adder_27_out_5), .out_4(adder_20_out_4),
    .out_5(adder_20_out_5));
  and and_15 (and_15_out, in_2[7], in_1[6]);
  adder adder_21 (
    .in_1(and_28_out), .in_2(adder_13_out_4), .in_3(adder_28_out_5), .out_4(out_4[4]), .out_5(adder_21_out_5));
  and and_16 (and_16_out, in_1[6], in_2[0]);
  and and_17 (and_17_out, in_1[5], in_2[1]);
  adder adder_22 (
    .in_1(and_31_out), .in_2(and_33_out), .in_3(adder_29_out_5), .out_4(adder_22_out_4),
    .out_5(adder_22_out_5));
  and and_18 (and_18_out, in_2[2], in_1[5]);
  and and_19 (and_19_out, in_2[2], in_1[4]);
  adder adder_23 (
    .in_1(and_19_out), .in_2(adder_15_out_4), .in_3(adder_30_out_5), .out_4(adder_23_out_4),
    .out_5(adder_23_out_5));
  and and_20 (and_20_out, in_2[3], in_1[4]);
  and and_21 (and_21_out, in_2[3], in_1[5]);
  adder adder_24 (
    .in_1(and_20_out), .in_2(adder_16_out_4), .in_3(adder_31_out_5), .out_4(adder_24_out_4),
    .out_5(adder_24_out_5));
  and and_22 (and_22_out, in_2[4], in_1[4]);
  and and_23 (and_23_out, in_2[4], in_1[5]);
  adder adder_25 (
    .in_1(and_22_out), .in_2(adder_17_out_4), .in_3(adder_32_out_5), .out_4(adder_25_out_4),
    .out_5(adder_25_out_5));
  and and_24 (and_24_out, in_2[5], in_1[4]);
  and and_25 (and_25_out, in_2[5], in_1[5]);
  adder adder_26 (
    .in_1(and_24_out), .in_2(adder_18_out_4), .in_3(adder_33_out_5), .out_4(adder_26_out_4),
    .out_5(adder_26_out_5));
  and and_26 (and_26_out, in_2[6], in_1[4]);
  and and_27 (and_27_out, in_2[6], in_1[5]);
  adder adder_27 (
    .in_1(and_26_out), .in_2(adder_19_out_4), .in_3(adder_34_out_5), .out_4(adder_27_out_4),
    .out_5(adder_27_out_5));
  and and_28 (and_28_out, in_2[7], in_1[5]);
  and and_29 (and_29_out, in_2[7], in_1[4]);
  adder adder_28 (
    .in_1(and_29_out), .in_2(adder_20_out_4), .in_3(adder_35_out_5), .out_4(out_4[3]), .out_5(adder_28_out_5));
  and and_30 (and_30_out, in_1[4], in_2[0]);
  and and_31 (and_31_out, in_1[5], in_2[0]);
  and and_32 (and_32_out, in_1[3], in_2[1]);
  and and_33 (and_33_out, in_1[4], in_2[1]);
  adder adder_29 (
    .in_1(and_30_out), .in_2(and_32_out), .in_3(adder_36_out_5), .out_4(adder_29_out_4),
    .out_5(adder_29_out_5));
  and and_34 (and_34_out, in_2[2], in_1[3]);
  adder adder_30 (
    .in_1(and_34_out), .in_2(adder_22_out_4), .in_3(adder_37_out_5), .out_4(adder_30_out_4),
    .out_5(adder_30_out_5));
  and and_35 (and_35_out, in_2[3], in_1[3]);
  adder adder_31 (
    .in_1(and_35_out), .in_2(adder_23_out_4), .in_3(adder_38_out_5), .out_4(adder_31_out_4),
    .out_5(adder_31_out_5));
  and and_36 (and_36_out, in_2[4], in_1[3]);
  adder adder_32 (
    .in_1(and_36_out), .in_2(adder_24_out_4), .in_3(adder_39_out_5), .out_4(adder_32_out_4),
    .out_5(adder_32_out_5));
  and and_37 (and_37_out, in_2[5], in_1[3]);
  adder adder_33 (
    .in_1(and_37_out), .in_2(adder_25_out_4), .in_3(adder_40_out_5), .out_4(adder_33_out_4),
    .out_5(adder_33_out_5));
  and and_38 (and_38_out, in_2[6], in_1[3]);
  adder adder_34 (
    .in_1(and_38_out), .in_2(adder_26_out_4), .in_3(adder_41_out_5), .out_4(adder_34_out_4),
    .out_5(adder_34_out_5));
  and and_39 (and_39_out, in_2[7], in_1[3]);
  adder adder_35 (
    .in_1(and_39_out), .in_2(adder_27_out_4), .in_3(adder_42_out_5), .out_4(out_4[2]), .out_5(adder_35_out_5));
  and and_40 (and_40_out, in_1[3], in_2[0]);
  and and_41 (and_41_out, in_1[2], in_2[1]);
  adder adder_36 (
    .in_1(and_40_out), .in_2(and_41_out), .in_3(adder_43_out_5), .out_4(adder_36_out_4),
    .out_5(adder_36_out_5));
  and and_42 (and_42_out, in_2[2], in_1[2]);
  adder adder_37 (
    .in_1(and_42_out), .in_2(adder_29_out_4), .in_3(adder_44_out_5), .out_4(adder_37_out_4),
    .out_5(adder_37_out_5));
  and and_43 (and_43_out, in_2[3], in_1[2]);
  adder adder_38 (
    .in_1(and_43_out), .in_2(adder_30_out_4), .in_3(adder_45_out_5), .out_4(adder_38_out_4),
    .out_5(adder_38_out_5));
  and and_44 (and_44_out, in_2[4], in_1[2]);
  adder adder_39 (
    .in_1(and_44_out), .in_2(adder_31_out_4), .in_3(adder_46_out_5), .out_4(adder_39_out_4),
    .out_5(adder_39_out_5));
  and and_45 (and_45_out, in_2[5], in_1[2]);
  adder adder_40 (
    .in_1(and_45_out), .in_2(adder_32_out_4), .in_3(adder_47_out_5), .out_4(adder_40_out_4),
    .out_5(adder_40_out_5));
  and and_46 (and_46_out, in_2[6], in_1[2]);
  adder adder_41 (
    .in_1(and_46_out), .in_2(adder_33_out_4), .in_3(adder_48_out_5), .out_4(adder_41_out_4),
    .out_5(adder_41_out_5));
  and and_47 (and_47_out, in_2[7], in_1[2]);
  adder adder_42 (
    .in_1(and_47_out), .in_2(adder_34_out_4), .in_3(adder_49_out_5), .out_4(out_4[1]), .out_5(adder_42_out_5));
  and and_48 (and_48_out, in_1[2], in_2[0]);
  and and_49 (and_49_out, in_1[1], in_2[1]);
  adder adder_43 (
    .in_1(and_48_out), .in_2(and_49_out), .in_3(adder_50_out_5), .out_4(adder_43_out_4),
    .out_5(adder_43_out_5));
  and and_50 (and_50_out, in_2[2], in_1[1]);
  and and_51 (and_51_out, in_2[2], in_1[0]);
  adder adder_44 (
    .in_1(and_50_out), .in_2(adder_36_out_4), .in_3(adder_51_out_5), .out_4(adder_44_out_4),
    .out_5(adder_44_out_5));
  and and_52 (and_52_out, in_2[3], in_1[1]);
  and and_53 (and_53_out, in_2[3], in_1[0]);
  adder adder_45 (
    .in_1(and_52_out), .in_2(adder_37_out_4), .in_3(adder_52_out_5), .out_4(adder_45_out_4),
    .out_5(adder_45_out_5));
  and and_54 (and_54_out, in_2[4], in_1[0]);
  and and_55 (and_55_out, in_2[4], in_1[1]);
  adder adder_46 (
    .in_1(and_55_out), .in_2(adder_38_out_4), .in_3(adder_53_out_5), .out_4(adder_46_out_4),
    .out_5(adder_46_out_5));
  and and_56 (and_56_out, in_2[5], in_1[0]);
  and and_57 (and_57_out, in_2[5], in_1[1]);
  adder adder_47 (
    .in_1(and_57_out), .in_2(adder_39_out_4), .in_3(adder_54_out_5), .out_4(adder_47_out_4),
    .out_5(adder_47_out_5));
  and and_58 (and_58_out, in_2[6], in_1[1]);
  and and_59 (and_59_out, in_2[6], in_1[0]);
  adder adder_48 (
    .in_1(and_58_out), .in_2(adder_40_out_4), .in_3(adder_55_out_5), .out_4(adder_48_out_4),
    .out_5(adder_48_out_5));
  and and_60 (and_60_out, in_2[7], in_1[1]);
  and and_61 (and_61_out, in_2[7], in_1[0]);
  adder adder_49 (
    .in_1(and_60_out), .in_2(adder_41_out_4), .in_3(adder_56_out_5), .out_4(out_4[0]), .out_5(adder_49_out_5));
  and and_62 (out_3[0], in_1[0], in_2[0]);
  and and_63 (and_63_out, in_1[1], in_2[0]);
  and and_64 (and_64_out, in_1[0], in_2[1]);
  adder adder_50 (.in_1(and_63_out), .in_2(and_64_out), .in_3(1'b0), .out_4(out_3[1]), .out_5(adder_50_out_5));
  adder adder_51 (.in_1(and_51_out), .in_2(adder_43_out_4), .in_3(1'b0), .out_4(out_3[2]), .out_5(adder_51_out_5));
  adder adder_52 (.in_1(and_53_out), .in_2(adder_44_out_4), .in_3(1'b0), .out_4(out_3[3]), .out_5(adder_52_out_5));
  adder adder_53 (.in_1(and_54_out), .in_2(adder_45_out_4), .in_3(1'b0), .out_4(out_3[4]), .out_5(adder_53_out_5));
  adder adder_54 (.in_1(and_56_out), .in_2(adder_46_out_4), .in_3(1'b0), .out_4(out_3[5]), .out_5(adder_54_out_5));
  adder adder_55 (.in_1(and_59_out), .in_2(adder_47_out_4), .in_3(1'b0), .out_4(out_3[6]), .out_5(adder_55_out_5));
  adder adder_56 (.in_1(and_61_out), .in_2(adder_48_out_4), .in_3(1'b0), .out_4(out_3[7]), .out_5(adder_56_out_5));

  // Other names for the same wires on the sheet: _8 = in_1[0]; _7 = in_1[1]; _6 = in_1[2]; _5 = in_1[3]; _4 = in_1[4];
  //   _3 = in_1[5]; _2 = in_1[6]; _1 = in_1[7]
endmodule

module multiply_8_bit_signed (
  input  [7:0] in_1,
  input  [7:0] in_2,
  output [7:0] R,
  output [7:0] R_2
);

  wire xor_1_out;
  wire [7:0] convert_straight_1_out_2, convert_straight_2_out_2, multiplier_1_cout, multiplier_1_out;
  wire [15:0] adder_1_out, not_1_out;

  convert_straight convert_straight_1 (.in_1(in_1), .out_2(convert_straight_1_out_2));
  convert_straight convert_straight_2 (.in_1(in_2), .out_2(convert_straight_2_out_2));
  xor xor_1 (xor_1_out, in_1[7], in_2[7]);
  Multiplier multiplier_1 (
    .a(convert_straight_1_out_2), .b(convert_straight_2_out_2), .out(multiplier_1_out),
    .cout(multiplier_1_cout));  // open: cin
  assign not_1_out = ~{multiplier_1_cout, multiplier_1_out};  // NOT_Gate not_1, 16 bits wide
  Multiplexer #(.width(16)) multiplexer_1 (
    .in0({multiplier_1_cout, multiplier_1_out}), .in1(adder_1_out), .out({R_2, R}), .sel(xor_1_out));  // open: en
  Adder #(.width(16)) adder_1 (.a(not_1_out), .b(16'h1), .out(adder_1_out));  // open: cin, cout
endmodule

module division2 (
  input  [7:0] in_1,
  input  [7:0] in_2,
  output [7:0] out_3,
  output out_4
);

  wire comparator_1_eq, comparator_1_lt, comparator_2_eq, comparator_2_lt, comparator_3_eq, comparator_3_lt,
       comparator_4_eq, comparator_4_lt, comparator_5_eq, comparator_5_lt, comparator_6_eq, comparator_6_lt,
       comparator_7_eq, comparator_7_lt, comparator_8_eq, comparator_8_lt, or_2_out, or_3_out, or_4_out,
       or_5_out, or_6_out, or_7_out, or_8_out, or_9_out;
  wire [7:0] multiplier_1_cout, multiplier_1_out, multiplier_2_cout, multiplier_2_out, multiplier_3_cout,
       multiplier_3_out, multiplier_4_cout, multiplier_4_out, multiplier_5_cout, multiplier_5_out,
       multiplier_6_cout, multiplier_6_out, multiplier_7_cout, multiplier_7_out, multiplier_8_out, or_1_out;

  Multiplier multiplier_1 (.a(in_2), .b(8'h80), .out(multiplier_1_out), .cout(multiplier_1_cout));  // open: cin
  assign or_1_out = in_2 | {8{1'b0}};  // OR_Gate or_1, 8 bits wide
  Comparator #(.mode("unsigned")) comparator_1 (
    .a(multiplier_1_out), .b(in_1), .eq(comparator_1_eq), .lt(comparator_1_lt));  // open: gt
  or or_2 (or_2_out, comparator_1_eq, comparator_1_lt);
  not not_1 (out_4, or_3_out);
  or or_3 (or_3_out, or_1_out[0], or_1_out[1], or_1_out[2], or_1_out[3], or_1_out[4], or_1_out[5], or_1_out[6], or_1_out[7]);
  overflow overflow_1 (.in_1(multiplier_1_cout), .in_2(or_2_out), .out_3(out_3[7]));
  Multiplier multiplier_2 (
    .a({out_3[7], 7'b1000000}), .b(in_2), .out(multiplier_2_out), .cout(multiplier_2_cout));  // open: cin
  Comparator #(.mode("unsigned")) comparator_2 (
    .a(multiplier_2_out), .b(in_1), .eq(comparator_2_eq), .lt(comparator_2_lt));  // open: gt
  overflow overflow_2 (.in_1(multiplier_2_cout), .in_2(or_4_out), .out_3(out_3[6]));
  or or_4 (or_4_out, comparator_2_eq, comparator_2_lt);
  Multiplier multiplier_3 (
    .a({out_3[7:6], 6'b100000}), .b(in_2), .out(multiplier_3_out), .cout(multiplier_3_cout));  // open: cin
  Comparator #(.mode("unsigned")) comparator_3 (
    .a(multiplier_3_out), .b(in_1), .eq(comparator_3_eq), .lt(comparator_3_lt));  // open: gt
  or or_5 (or_5_out, comparator_3_eq, comparator_3_lt);
  overflow overflow_3 (.in_1(multiplier_3_cout), .in_2(or_5_out), .out_3(out_3[5]));
  Multiplier multiplier_4 (
    .a({out_3[7:5], 5'b10000}), .b(in_2), .out(multiplier_4_out), .cout(multiplier_4_cout));  // open: cin
  Comparator #(.mode("unsigned")) comparator_4 (
    .a(multiplier_4_out), .b(in_1), .eq(comparator_4_eq), .lt(comparator_4_lt));  // open: gt
  overflow overflow_4 (.in_1(multiplier_4_cout), .in_2(or_6_out), .out_3(out_3[4]));
  or or_6 (or_6_out, comparator_4_eq, comparator_4_lt);
  Multiplier multiplier_5 (
    .a({out_3[7:4], 4'b1000}), .b(in_2), .out(multiplier_5_out), .cout(multiplier_5_cout));  // open: cin
  Comparator #(.mode("unsigned")) comparator_5 (
    .a(multiplier_5_out), .b(in_1), .eq(comparator_5_eq), .lt(comparator_5_lt));  // open: gt
  overflow overflow_5 (.in_1(multiplier_5_cout), .in_2(or_7_out), .out_3(out_3[3]));
  or or_7 (or_7_out, comparator_5_eq, comparator_5_lt);
  Multiplier multiplier_6 (
    .a({out_3[7:3], 3'b100}), .b(in_2), .out(multiplier_6_out), .cout(multiplier_6_cout));  // open: cin
  overflow overflow_6 (.in_1(multiplier_6_cout), .in_2(or_8_out), .out_3(out_3[2]));
  Comparator #(.mode("unsigned")) comparator_6 (
    .a(multiplier_6_out), .b(in_1), .eq(comparator_6_eq), .lt(comparator_6_lt));  // open: gt
  or or_8 (or_8_out, comparator_6_eq, comparator_6_lt);
  Multiplier multiplier_7 (
    .a({out_3[7:2], 2'b10}), .b(in_2), .out(multiplier_7_out), .cout(multiplier_7_cout));  // open: cin
  Comparator #(.mode("unsigned")) comparator_7 (
    .a(multiplier_7_out), .b(in_1), .eq(comparator_7_eq), .lt(comparator_7_lt));  // open: gt
  or or_9 (or_9_out, comparator_7_eq, comparator_7_lt);
  overflow overflow_7 (.in_1(multiplier_7_cout), .in_2(or_9_out), .out_3(out_3[1]));
  Multiplier multiplier_8 (.a({out_3[7:1], 1'b1}), .b(in_2), .out(multiplier_8_out));  // open: cin, cout
  Comparator #(.mode("unsigned")) comparator_8 (
    .a(multiplier_8_out), .b(in_1), .eq(comparator_8_eq), .lt(comparator_8_lt));  // open: gt
  or or_10 (out_3[0], comparator_8_eq, comparator_8_lt);
endmodule

module overflow (
  input  [7:0] in_1,
  input  in_2,
  output out_3
);

  wire or_1_out;

  or or_1 (or_1_out, in_1[0], in_1[1], in_1[2], in_1[3], in_1[4], in_1[5], in_1[6], in_1[7]);
  Transistor transistor_1 (.in(in_2), .out(out_3), .gate(or_1_out));
  Pull_Resistor pull_resistor_1 (.node(out_3));
endmodule

module division2_signed (
  input  [7:0] in_1,
  input  [7:0] in_2,
  output [7:0] R
);

  wire xor_1_out;
  wire [7:0] adder_1_out, convert_straight_1_out_2, convert_straight_2_out_2, division2_1_out_3, not_1_out;

  convert_straight convert_straight_1 (.in_1(in_1), .out_2(convert_straight_1_out_2));
  convert_straight convert_straight_2 (.in_1(in_2), .out_2(convert_straight_2_out_2));
  xor xor_1 (xor_1_out, in_1[7], in_2[7]);
  division2 division2_1 (
    .in_1(convert_straight_1_out_2), .in_2(convert_straight_2_out_2), .out_3(division2_1_out_3));  // open: out_4
  assign not_1_out = ~division2_1_out_3;  // NOT_Gate not_1, 8 bits wide
  Multiplexer #(.width(8)) multiplexer_1 (
    .in0(division2_1_out_3), .in1(adder_1_out), .out(R), .sel(xor_1_out));  // open: en
  Adder adder_1 (.a(not_1_out), .b(8'h1), .out(adder_1_out));  // open: cin, cout
endmodule

module cmp_float (
  input  [16:0] in_1,
  input  [16:0] in_2,
  output out_3,
  output out_4,
  output out_5,
  output out_6,
  output out_7,
  output out_8
);

  wire and_1_out, and_2_out, and_3_out, and_4_out, and_5_out, and_6_out, cmp8_no_sign_1_out_3,
       cmp8_no_sign_1_out_4, cmp8_no_sign_1_out_5, cmp8_no_sign_2_out_3, cmp8_no_sign_2_out_4,
       cmp8_no_sign_2_out_5, isinfinity_1_r, isinfinity_2_r, isnan_1_r, not_1_out_2, not_2_out_2,
       not_3_out_2, not_4_out_2, not_5_out, not_6_out, not_7_out, not_8_out, not_9_out, or_1_out, or_2_out,
       \З_out_3 , \З_out_4 , \З_out_5 , \Ноль_out ;

  NOT not_1 (.in_1(in_1[15:8]), .out_2(not_1_out_2));
  NOT not_2 (.in_1(in_1[7:0]), .out_2(not_2_out_2));
  NOT not_3 (.in_1(in_2[7:0]), .out_2(not_3_out_2));
  NOT not_4 (.in_1(in_2[15:8]), .out_2(not_4_out_2));
  cmp8_no_sign cmp8_no_sign_1 (
    .in_1(in_1[15:8]), .in_2(in_2[15:8]), .out_3(cmp8_no_sign_1_out_3), .out_4(cmp8_no_sign_1_out_4),
    .out_5(cmp8_no_sign_1_out_5));
  cmp8_no_sign cmp8_no_sign_2 (
    .in_1(in_1[7:0]), .in_2(in_2[7:0]), .out_3(cmp8_no_sign_2_out_3), .out_4(cmp8_no_sign_2_out_4),
    .out_5(cmp8_no_sign_2_out_5));
  cmp1 \u_З  (.in_1(not_5_out), .in_2(not_6_out), .out_3(\З_out_3 ), .out_4(\З_out_4 ), .out_5(\З_out_5 ));
  not not_5 (not_5_out, in_1[16]);
  not not_6 (not_6_out, in_2[16]);
  and \u_Ноль  (\Ноль_out , not_1_out_2, not_2_out_2, not_3_out_2, not_4_out_2);
  isNan isnan_1 (.M1(in_1[7:0]), .\П1 (in_1[15:8]), .\М2 (in_2[7:0]), .\П2 (in_2[15:8]), .R(isnan_1_r));
  isInfinity isinfinity_1 (.M1(in_2[7:0]), .\П1 (in_2[15:8]), .R(isinfinity_1_r));
  isInfinity isinfinity_2 (.M1(in_1[7:0]), .\П1 (in_1[15:8]), .R(isinfinity_2_r));
  not not_7 (not_7_out, isnan_1_r);
  and and_1 (and_1_out, isinfinity_1_r, isinfinity_2_r, \З_out_4 );
  not not_8 (not_8_out, and_1_out);
  and and_2 (and_2_out, \З_out_4 , cmp8_no_sign_1_out_4);
  and and_3 (and_3_out, \З_out_4 , cmp8_no_sign_1_out_3, cmp8_no_sign_2_out_4);
  and and_4 (and_4_out, \З_out_4 , cmp8_no_sign_1_out_5);
  and and_5 (and_5_out, \З_out_4 , cmp8_no_sign_1_out_3, cmp8_no_sign_2_out_5);
  and and_6 (and_6_out, not_8_out, not_7_out, cmp8_no_sign_1_out_3, cmp8_no_sign_2_out_3, \З_out_4 );
  not not_9 (not_9_out, out_4);
  or or_1 (or_1_out, \З_out_5 , and_2_out, and_3_out);
  or or_2 (or_2_out, \З_out_3 , and_4_out, and_5_out);
  or or_3 (out_4, \Ноль_out , and_6_out);
  and and_7 (out_5, not_9_out, or_1_out);
  and and_8 (out_7, not_9_out, or_2_out);
  not not_10 (out_3, out_4);
  or or_4 (out_6, out_4, out_7);
  or or_5 (out_8, out_4, out_5);

  // Notes on the sheet:
  //   0 = 10..00
  //   1=10..01
  //   -1=01..11
  //   1,
  //   1,
  //   экспонента - код со сдвигом
  //   bit 16 - sign
  //   bits 8-13 - exponent
  //   bits 0-7 - mantis
  //   (-1)^S * M * B^e
endmodule

module cmp8_no_sign (
  input  [7:0] in_1,
  input  [7:0] in_2,
  output out_3,
  output out_4,
  output out_5
);

  Comparator #(.mode("unsigned")) comparator_1 (.a(in_1), .b(in_2), .gt(out_4), .eq(out_3), .lt(out_5));
endmodule

module isNan (
  input  [7:0] M1,
  input  [7:0] \П1 ,
  input  [7:0] \М2 ,
  input  [7:0] \П2 ,
  output R
);

  wire all_bits_1s_1_r, all_bits_1s_2_r, and_1_out, and_2_out, not_1_out_2, not_2_out, not_3_out, not_4_out_2;

  NOT not_1 (.in_1(M1), .out_2(not_1_out_2));
  not not_2 (not_2_out, not_1_out_2);
  all_bits_1s all_bits_1s_1 (.in_1(\П1 ), .R(all_bits_1s_1_r));
  not not_3 (not_3_out, not_4_out_2);
  NOT not_4 (.in_1(\М2 ), .out_2(not_4_out_2));
  all_bits_1s all_bits_1s_2 (.in_1(\П2 ), .R(all_bits_1s_2_r));
  and and_1 (and_1_out, not_2_out, all_bits_1s_1_r);
  or or_1 (R, and_1_out, and_2_out);
  and and_2 (and_2_out, not_3_out, all_bits_1s_2_r);
endmodule

module all_bits_1s (
  input  [7:0] in_1,
  output R
);

  and and_1 (R, in_1[0], in_1[1], in_1[2], in_1[3], in_1[4], in_1[5], in_1[6], in_1[7]);
endmodule

module isInfinity (
  input  [7:0] M1,
  input  [7:0] \П1 ,
  output R
);

  wire all_bits_1s_1_r, not_1_out_2;

  NOT not_1 (.in_1(M1), .out_2(not_1_out_2));
  all_bits_1s all_bits_1s_1 (.in_1(\П1 ), .R(all_bits_1s_1_r));
  and and_1 (R, not_1_out_2, all_bits_1s_1_r);
endmodule
