// Logisim project baranov2.circ as structural Verilog: 5 circuits, main circuit RS
module RS (
  input  Reset,
  input  Set,
  output Q,
  output not_Q
);

  nor nor_1 (Q, Reset, not_Q);
  nor nor_2 (not_Q, Q, Set);
endmodule

module D (
  input  Clock,
  input  Data,
  output out_3,
  output out_4
);

  wire and_1_out, and_2_out, not_1_out;

  and and_1 (and_1_out, Clock, not_1_out);
  not not_1 (not_1_out, Data);
  and and_2 (and_2_out, Clock, Data);
  RS rs_1 (.Reset(and_1_out), .Set(and_2_out), .Q(out_3), .not_Q(out_4));
endmodule

module D_flip_flop (
  input  in_1,
  input  Data,
  output out_3
);

  wire d_1_out_3, not_1_out;

  not not_1 (not_1_out, in_1);
  D d_1 (.Clock(not_1_out), .Data(Data), .out_3(d_1_out_3));  // open: out_4
  D d_2 (.Clock(in_1), .Data(d_1_out_3), .out_3(out_3));  // open: out_4

  // Notes on the sheet:
  //   Clock
endmodule

module _8_bit_register (
  input  in_1,
  input  in_2,
  input  [7:0] in_3,
  output [7:0] out_4
);

  wire and_1_out;

  D_flip_flop d_flip_flop_1 (.in_1(and_1_out), .Data(in_3[0]), .out_3(out_4[0]));
  D_flip_flop d_flip_flop_2 (.in_1(and_1_out), .Data(in_3[1]), .out_3(out_4[1]));
  D_flip_flop d_flip_flop_3 (.in_1(and_1_out), .Data(in_3[2]), .out_3(out_4[2]));
  D_flip_flop d_flip_flop_4 (.in_1(and_1_out), .Data(in_3[3]), .out_3(out_4[3]));
  D_flip_flop d_flip_flop_5 (.in_1(and_1_out), .Data(in_3[4]), .out_3(out_4[4]));
  D_flip_flop d_flip_flop_6 (.in_1(and_1_out), .Data(in_3[5]), .out_3(out_4[5]));
  D_flip_flop d_flip_flop_7 (.in_1(and_1_out), .Data(in_3[6]), .out_3(out_4[6]));
  D_flip_flop d_flip_flop_8 (.in_1(and_1_out), .Data(in_3[7]), .out_3(out_4[7]));
  and and_1 (and_1_out, in_2, in_1);
endmodule

module tact_cntr (
  input  in_1,
  input  [7:0] in_2,
  output [7:0] out_3
);

  wire adder_1_cout, and_1_out, clock_1_out, not_1_out, not_2_out, or_1_out;
  wire [7:0] transistor_1_out, transistor_2_out;

  not not_1 (not_1_out, in_1);
  Clock clock_1 (.out(clock_1_out));
  or or_1 (or_1_out, in_1, not_2_out);
  not not_2 (not_2_out, adder_1_cout);
  Transistor #(.width(8)) transistor_1 (.in(transistor_2_out), .out(transistor_1_out), .gate(in_1));
  Transistor #(.width(8)) transistor_2 (.in(in_2), .out(transistor_2_out), .gate(not_1_out));
  Register register_1 (.D(transistor_2_out), .Q(out_3), .clk(and_1_out));  // open: en, clr
  and and_1 (and_1_out, clock_1_out, or_1_out);
  Adder adder_1 (.a(8'h1), .b(out_3), .out(transistor_1_out), .cout(adder_1_cout));  // open: cin
endmodule
